// Digital circuit 74ls393.dig as structural Verilog
// 4-bit Binary Counter.
// Connect QA to CKB and clock on CKA for full 4-bit counter.  Connect QB to R1 and QD to R2 for a BCD counter.
module _74ls393 (
  input  CKA,
  input  VCC,
  input  GND,
  input  _1CLR,
  input  CKB,
  input  _2CLR,
  output _1QA,
  output _1QB,
  output _1QC,
  output _1QD,
  output _2QA,
  output _2QB,
  output _2QC,
  output _2QD
);

  wire not_1_out, not_2_out;

  not not_1 (not_1_out, _1CLR);
  PowerSupply powersupply_1 (.VDD(VCC), .GND(GND));
  JK_FF_AS jk_ff_as_1 (.Set(1'b0), .J(1'b1), .C(~CKA), .K(1'b1), .Clr(~not_1_out), .Q(_1QA));  // open: nQ
  JK_FF_AS jk_ff_as_2 (.Set(1'b0), .J(1'b1), .C(~_1QA), .K(1'b1), .Clr(~not_1_out), .Q(_1QB));  // open: nQ
  JK_FF_AS jk_ff_as_3 (.Set(1'b0), .J(1'b1), .C(~_1QB), .K(1'b1), .Clr(~not_1_out), .Q(_1QC));  // open: nQ
  JK_FF_AS jk_ff_as_4 (.Set(1'b0), .J(1'b1), .C(~_1QC), .K(1'b1), .Clr(~not_1_out), .Q(_1QD));  // open: nQ
  not not_2 (not_2_out, _2CLR);
  JK_FF_AS jk_ff_as_5 (.Set(1'b0), .J(1'b1), .C(~CKB), .K(1'b1), .Clr(~not_2_out), .Q(_2QA));  // open: nQ
  JK_FF_AS jk_ff_as_6 (.Set(1'b0), .J(1'b1), .C(~_2QA), .K(1'b1), .Clr(~not_2_out), .Q(_2QB));  // open: nQ
  JK_FF_AS jk_ff_as_7 (.Set(1'b0), .J(1'b1), .C(~_2QB), .K(1'b1), .Clr(~not_2_out), .Q(_2QC));  // open: nQ
  JK_FF_AS jk_ff_as_8 (.Set(1'b0), .J(1'b1), .C(~_2QC), .K(1'b1), .Clr(~not_2_out), .Q(_2QD));  // open: nQ

  // Notes on the sheet:
  //   CKA: Clock A input, pin 1
  //   _1QA: Bit 0 (LSB) of 4-bit counter, pin 3
  //   _1QB: Bit 1 of 4-bit counter, pin 4
  //   _1QC: Bit 2 of 4-bit counter, pin 5
  //   _1QD: Bit 3 (MSB) of 4-bit counter, pin 6
  //   VCC: pin 14, default 1
  //   GND: pin 7
  //   _1CLR: pin 2
  //   CKB: Clock A input, pin 13
  //   _2QA: Bit 0 (LSB) of 4-bit counter, pin 11
  //   _2QB: Bit 1 of 4-bit counter, pin 10
  //   _2QC: Bit 2 of 4-bit counter, pin 9
  //   _2QD: Bit 3 (MSB) of 4-bit counter, pin 8
  //   _2CLR: pin 12
endmodule
