// Digital circuit 74ls393_b.dig as structural Verilog
module _74ls393_b (
  input  in_1,
  input  in_2,
  output out_3,
  output out_4,
  output out_5,
  output out_6
);

  wire t_ff_1_q, t_ff_2_q, t_ff_3_q, t_ff_4_q;

  T_FF t_ff_1 (.T(in_1), .C(in_2), .Q(t_ff_1_q), .nQ(out_3));
  T_FF t_ff_2 (.T(t_ff_1_q), .C(in_2), .Q(t_ff_2_q), .nQ(out_4));
  T_FF t_ff_3 (.T(t_ff_2_q), .C(in_2), .Q(t_ff_3_q), .nQ(out_5));
  T_FF t_ff_4 (.T(t_ff_3_q), .C(in_2), .Q(t_ff_4_q), .nQ(out_6));
  LED led_1 (.in(t_ff_1_q));
  LED led_2 (.in(t_ff_2_q));
  LED led_3 (.in(t_ff_3_q));
  LED led_4 (.in(t_ff_4_q));
endmodule
