// Digital circuit address_display_driver.dig as structural Verilog
module address_display_driver (
  input  [6:0] RAS_ADDR,
  input  nENRAS,
  input  [6:0] CAS_ADDR,
  input  nENCAS,
  input  nRAS,
  output [3:0] HEX0,
  output [3:0] HEX1,
  output [3:0] HEX2,
  output [3:0] HEX3
);

  wire and_1_out, and_2_out;

  and and_1 (and_1_out, nRAS, ~nENRAS);  // And
  D_FF #(.Bits(7)) d_ff_1 (.D(RAS_ADDR), .C(~and_1_out), .Q({HEX1[2:0], HEX0}));  // open: nQ
  and and_2 (and_2_out, nRAS, ~nENCAS);  // And
  D_FF #(.Bits(7)) d_ff_2 (.D(CAS_ADDR), .C(and_2_out), .Q({HEX3[1:0], HEX2, HEX1[3]}));  // open: nQ

  assign HEX3[3:2] = 2'b00;

  // Notes on the sheet:
  //   nENRAS: default 1
  //   nENCAS: default 1
endmodule
