// Digital circuit blink_circuit.dig as structural Verilog
module blink_circuit (
  input  BLINK_EN,
  input  AT7,
  input  nBLINK,
  input  CHG_DOTS,
  input  nBLINK_CURSOR,
  input  nCURSOR_DLY
);

  wire and_1_out, nand_1_out, nor_1_out, or_1_out, or_2_out;

  nand nand_1 (nand_1_out, nCURSOR_DLY, BLINK_EN, AT7);
  or or_1 (or_1_out, nBLINK, nand_1_out);
  LED led_1 (.in(nand_1_out));
  nor nor_1 (nor_1_out, nBLINK_CURSOR, nCURSOR_DLY);
  and and_1 (and_1_out, CHG_DOTS, or_1_out);
  LED led_2 (.in(nor_1_out));
  LED led_3 (.in(and_1_out));
  or or_2 (or_2_out, nor_1_out, and_1_out);
  LED led_4 (.in(or_2_out));
endmodule
