// Digital circuit blink_logic.dig as structural Verilog
module blink_logic (
  input  BLINK_EN,
  input  AT7,
  input  nBLINK,
  input  CHG_DOTS,
  input  nBLINK_CURSOR,
  input  nCURSOR_DLY
);

  wire and_1_out, nand_1_out, nor_1_out, or_1_out, or_2_out;

  nand nand_1 (nand_1_out, nCURSOR_DLY, BLINK_EN, AT7);
  or or_1 (or_1_out, nBLINK, nand_1_out);
  LED led_1 (.in(nand_1_out));
  nor nor_1 (nor_1_out, nBLINK_CURSOR, nCURSOR_DLY);
  and and_1 (and_1_out, CHG_DOTS, or_1_out);
  LED led_2 (.in(nor_1_out));
  LED led_3 (.in(and_1_out));
  or or_2 (or_2_out, nor_1_out, and_1_out);
  LED led_4 (.in(or_2_out));

  // Notes on the sheet:
  //   If the cursor is not visible, text blinking is enabled,
  //   and blink attribute is set, draw alpha dots
  //   If the cursor is visible, and we are blinking the cursor, 
  //   draw alpha dots
  //   If we have character dots
  //   If Text isn't blinking
  //   If we have character dots and text isn't blinking,
  //   draw alpha dots
endmodule
