// Digital circuit cga.dig as structural Verilog
module cga (
);

  wire U33_d2;

  // _74112 U1: pin names not known
  // _7400 U25: pin names not known
  // _7404 U29: pin names not known
  // _7400 U46: pin names not known
  // _7474 U2: pin names not known
  // _7404 U26: pin names not known
  // _7432 U30: pin names not known
  // _7451 U47: pin names not known
  // _7486 U3: pin names not known
  // _7451 U27: pin names not known
  // _7408 U31: pin names not known
  // _7451 U48: pin names not known
  // _74174 U4: pin names not known
  // _7410 U28: pin names not known
  // _74166 U32: pin names not known
  // _7402 U49: pin names not known
  // _74174 U5: pin names not known
  mk36000 U33 (
    .D2(U33_d2), .GND(U33_d2));  // open: nCE, A0, A1, A2, A3, A4, A5, A6, A7, A8, A9, A10, A11, A12, D0, D1, D3, D4, D5, D6, D7, VCC
  // _7404 U6: pin names not known
  // _74374 U34: pin names not known
  // _74166 U7: pin names not known
  // _74166 U8: pin names not known
  // _74273 U35: pin names not known
  // _74153 U9: pin names not known
  // _74244 U36: pin names not known
  // _74153 U10: pin names not known
  // _74374 U37: pin names not known
  // _74174 U11: pin names not known
  mc6845 U38 ();  // open: VSS, VCC, nRESET, LPSTB, CLK, R_nW, E, RS, nCS, MA0, MA1, MA2, MA3, MA4, MA5, MA6, MA7, MA8, MA9, MA10, MA11, MA12, MA13, DEN, CUR, RA0, RA1, RA2, RA3, RA4, D7, D6, D5, D4, D3, D2, D1, D0, HS, VS
  _74ls393 U12 ();  // open: CKA, _1QA, _1QB, _1QC, _1QD, VCC, GND, _1CLR, CKB, _2QA, _2QB, _2QC, _2QD, _2CLR
  // _7408 U13: pin names not known
  // _74174 U101: pin names not known
  // _7432 U14: pin names not known
  // _74374 U58: pin names not known
  // _7400 U15: pin names not known
  // _74374 U59: pin names not known
  // _7404 U16: pin names not known
  // _74174 U39: pin names not known
  // _74374 U60: pin names not known
  // _74138 U17: pin names not known
  // _74174 U40: pin names not known
  // _74374 U61: pin names not known
  // _74138 U18: pin names not known
  // _74138 U19: pin names not known
  // _7408 U41: pin names not known
  // _74125 U62: pin names not known
  // _7404 U20: pin names not known
  // _7486 U42: pin names not known
  // _74175 U63: pin names not known
  // _74174 U21: pin names not known
  // _7474 U43: pin names not known
  // _74164 U64: pin names not known
  // _7451 U22: pin names not known
  // _7474 U44: pin names not known
  // _7402 U65: pin names not known
  // _7432 U23: pin names not known
  // _74151 U45: pin names not known
  // _74245 U66: pin names not known
  // _74244 U24: pin names not known
  // _7486 U68: pin names not known
  // _74244 U67: pin names not known
  VGA vga_1 ();  // open: R, G, B, H, V, C
endmodule
