// Digital circuit cga_16.dig as structural Verilog
module cga_16 (
  input  B,
  input  C,
  input  D,
  input  E,
  input  F,
  input  G,
  input  H,
  input  A2,
  input  clk,
  input  in_14,
  input  in_15,
  input  in_16,
  input  in_17,
  input  in_18,
  input  in_19,
  input  in_20,
  input  in_21,
  input  in_22,
  input  in_23,
  input  in_24,
  input  in_25,
  output [2:0] Y,
  output [5:0] X,
  output Z,
  output U
);

  wire _1Y_U3, _2Q_U48, _14MHZ, A0, and_2_out, AT7, AT_BLINK_GATE, B_OUT, B_t, BLUE, C0, C1, CAS_CC, CB_U43,
       CLK_COLOR, CLK_DOT, CURSOR, CYAN, DEN, DOTS_ALPHA, DOTS_CHG, edge_pulse_1_pulse, G_OUT, G_t, GREEN,
       HCLK, HRES_BORDER, HS, HSYNC_DLY, HSYNC_OUT, HSYNC_OUT_t, I, I_OUT, isa_slot_1_t_c, LATCH_AT,
       LATCH_CC, LCLK, MA12, MA12_COND, MAGENTA, MUX_A, MUX_B, n3_n58MHZ, n7MHZ, n14MHZ, nand_3_out,
       nand_4_out, nBLANK, nBLINK, nBLINK_EN, nBW_1, nBW_2, nCAS, nCLK_C, nCLR_SR, nCS_CROM, nCURSOR_BLINK,
       nCURSOR_DLY, nDEN, nDISPEN_DLY, nEN_COLOR, nENCAS_CPU, nENCAS_CRT, nENRAS_CPU, nENRAS_CRT, nGRPH,
       nHCLK, nHRES, nHRES_GFX, nIOW, nLCLK, nor_1_out, nor_2_out, not_1_out, not_3_out, not_8_out, nQ2,
       nRAS, nRESET, nRESET_t, or_1_out, OSC, pincontrol_1_p1, pincontrol_1_p4, pincontrol_2_p3,
       pincontrol_3_p4, pincontrol_4_p4, pincontrol_5_p4, pincontrol_6_p4, pincontrol_7_p4, pincontrol_8_p4,
       Q0_U64, Q1, Q2, Q2_U4, Q2_U64, Q3_U64, Q4, Q4_U64, Q5, Q5_U64, Q6_U64, Q7_U64, R, R_OUT, RAS, RED,
       RESET, SEL_BLUE, SL, SL_t, STR, U1_p15, U3_p13, U4__74LS174_p6, U4__74LS174_p16, U5__74S174_p4,
       U5__74S174_p7, U5__74S174_p14, U5__74S174_p16, U13_pin11, U13_pin12, U20__7404_p3, U20__7404_p9,
       U21__74174_p7, U21__74174_p8, U22_p1, U22_p13, U25_pin1, U25_pin3, U25_pin13, U26_pin8, U30_pin6,
       U43_pin5, U45_pin9, U45_pin10, U46_pin1, U46_pin2, U46_pin9, U46_pin13, U48_2_pin8, U49_pin1, U58_p9,
       U58_p10, U59_p10, U62_pin8, U63_pin2, U63_pin7, U63_pin10, U63_pin14, U64_pin1, U68_pin8, U101_p8, VS,
       VSYNC_DLY, VSYNC_OUT, VSYNC_OUT_t, YELLOW_BURST;
  wire [1:0] BG_p1, BG_p2, BG_p3, led_driver4_1_b_out, led_driver4_1_g_out, led_driver4_1_r_out,
       led_driver4_2_b_out, led_driver4_2_g_out, led_driver4_2_r_out;
  wire [3:0] AT_Splitter_even, AT_Splitter_odd, CC_Splitter_even, CC_Splitter_odd, color_shift_reg_1__0,
       color_shift_reg_1__1, color_shift_reg_1__2, color_shift_reg_1__3, color_shift_reg_1__4,
       color_shift_reg_1__5, color_shift_reg_1__6, color_shift_reg_1__7, RGBI, U32_pin2;
  wire [4:0] RA;
  wire [6:0] ADDR_CAS, AT_BUS;
  wire [7:0] CC_BUS, isa_slot_1_sd, MD_BUS, pincontrol_2_p1;
  wire [7:4] U32_pin10;
  wire [9:0] counter_1_out;
  wire [10:0] counter_2_out;
  wire [11:0] MA_BUS;
  wire [19:1] isa_slot_1_sa;

  not not_1 (not_1_out, Q5);
  _7400 U25 (
    .pin1(U25_pin1), .pin2(CLK_DOT), .pin3(U25_pin3), .pin4(1'b0), .pin5(1'b0), .pin7(1'b0), .pin9(1'b1),
    .pin10(1'b1), .pin11(U25_pin1), .pin12(U25_pin3), .pin13(U25_pin13), .pin14(1'b1));  // open: pin6, pin8
  _7400 U46 (
    .pin1(U46_pin1), .pin2(U46_pin2), .pin3(nENRAS_CPU), .pin4(U46_pin1), .pin5(U46_pin2), .pin6(nENCAS_CPU),
    .pin7(1'b0), .pin8(nENRAS_CRT), .pin9(U46_pin9), .pin10(U46_pin2), .pin11(nENCAS_CRT), .pin12(U46_pin9),
    .pin13(U46_pin13), .pin14(1'b1));
  // _74112 U1: pin names not known; wires that end beside it: 1'b1, RAS, _14MHZ, nRAS, 1'b1, 1'b1, Q5, _14MHZ, not_1_out, 1'b1, 1'b1, 1'b0, U46_pin13, U46_pin2, U1_p15
  not not_2 (U46_pin1, U46_pin9);
  nand nand_1 (LATCH_CC, U30_pin6, CAS_CC);
  _7404 U26 (
    .pin1(1'b1), .pin3(1'b1), .pin5(1'b1), .pin7(1'b0), .pin8(U26_pin8), .pin9(_2Q_U48), .pin10(U25_pin13),
    .pin11(CLK_DOT), .pin13(1'b1), .pin14(1'b1));  // open: pin2, pin4, pin6, pin12
  _7432 U30 (
    .pin1(1'b0), .pin2(1'b0), .pin4(nCLK_C), .pin5(in_14), .pin6(U30_pin6), .pin7(1'b0), .pin9(1'b0),
    .pin10(1'b0), .pin12(1'b0), .pin13(1'b0), .pin14(1'b1));  // open: pin3, pin8, pin11
  _7451 U47 (
    .pin1(in_15), .pin2(in_15), .pin3(in_14), .pin4(Q1), .pin5(nHRES), .pin6(U46_pin9), .pin7(1'b0),
    .pin8(LATCH_AT), .pin9(nGRPH), .pin10(1'b1), .pin11(nCLK_C), .pin12(nQ2), .pin13(1'b1), .pin14(1'b1));
  or or_1 (or_1_out, U26_pin8, nHRES_GFX);
  _7451 U48 (
    .pin1(1'b1), .pin2(C0), .pin3(U25_pin3), .pin4(C1), .pin5(U25_pin1), .pin6(_2Q_U48), .pin7(1'b0),
    .pin9(1'b1), .pin10(1'b1), .pin11(1'b1), .pin12(1'b1), .pin13(1'b1), .pin14(1'b1));  // open: pin8
  // _7486 U3: pin names not known; wires that end beside it: Q2, nLCLK, Q1, nLCLK, nLCLK, U1_p15, Q2_U4, Q4, 1'b1, 1'b0, _1Y_U3, RAS, U3_p13, CAS_CC
  _7451 U27 (
    .pin1(n7MHZ), .pin2(in_14), .pin3(HCLK), .pin4(nHRES), .pin5(LCLK), .pin6(nCLK_C), .pin7(1'b0),
    .pin8(CLK_DOT), .pin9(in_14), .pin10(1'b1), .pin11(n14MHZ), .pin12(nHRES), .pin13(1'b1), .pin14(1'b1));
  not not_3 (not_3_out, CAS_CC);
  not not_4 (nRAS, RAS);
  and and_1 (nCAS, U3_p13, not_3_out);
  // Probe on nCLK_C
  // _74174 U4__74LS174: pin names not known; wires that end beside it: nQ2, _14MHZ, nLCLK, Q2_U4, nRESET_t, U4__74LS174_p6, Q4, Q5, 1'b1, 1'b0, nLCLK, Q2_U4, U4__74LS174_p6, Q4, Q5, U4__74LS174_p16
  _7410 U28 (
    .pin1(HRES_BORDER), .pin2(nBLANK), .pin3(1'b0), .pin4(1'b0), .pin5(1'b0), .pin7(1'b0),
    .pin8(AT_BLINK_GATE), .pin9(nCURSOR_DLY), .pin10(in_19), .pin11(AT7), .pin12(STR), .pin13(or_1_out),
    .pin14(1'b1));  // open: pin6
  _74166 U32 (
    .pin1(1'b0), .pin2(U32_pin2[0]), .pin3(U32_pin2[1]), .pin4(U32_pin2[2]), .pin5(U32_pin2[3]), .pin6(1'b0),
    .pin7(CLK_DOT), .pin8(1'b0), .pin9(nCLR_SR), .pin10(U32_pin10[4]), .pin11(U32_pin10[5]),
    .pin12(U32_pin10[6]), .pin13(DOTS_CHG), .pin14(U32_pin10[7]), .pin15(SL), .pin16(1'b1));
  _7451 U48_2 (
    .pin1(RA[0]), .pin2(1'b0), .pin3(1'b0), .pin4(1'b0), .pin5(1'b0), .pin7(1'b0), .pin8(U48_2_pin8),
    .pin9(MA12), .pin10(1'b1), .pin11(nGRPH), .pin12(in_15), .pin13(1'b1), .pin14(1'b1));  // open: pin6
  // _74174 U5__74S174: pin names not known; wires that end beside it: U4__74LS174_p16, _14MHZ, Q1, U5__74S174_p4, nRESET_t, n7MHZ, U5__74S174_p7, nQ2, 1'b1, 1'b0, Q1, Q2, HCLK, U5__74S174_p14, n3_n58MHZ, U5__74S174_p16
  _7402 U49 (
    .pin1(U49_pin1), .pin2(Q2_U4), .pin3(in_14), .pin5(1'b0), .pin6(1'b0), .pin7(1'b0), .pin8(U48_2_pin8),
    .pin9(U48_2_pin8), .pin10(MA12_COND), .pin11(1'b0), .pin12(1'b0), .pin14(1'b1));  // open: pin4, pin13
  // _7404 U6__7404: pin names not known; wires that end beside it: nLCLK, U5__74S174_p16, U5__74S174_p14, HCLK, Q2, _14MHZ, 1'b1, 1'b0, LCLK, U5__74S174_p7, n7MHZ, nHCLK, nQ2, n14MHZ
  mk36000 U33 (
    .A0(RA[0]), .A1(RA[1]), .nCE(nCS_CROM), .A2(RA[2]), .A3(CC_BUS[0]), .A4(CC_BUS[1]), .A5(CC_BUS[2]),
    .A6(CC_BUS[3]), .A7(CC_BUS[4]), .A8(CC_BUS[5]), .A9(CC_BUS[6]), .A10(CC_BUS[7]), .A11(1'b1), .A12(1'b1),
    .VCC(1'b1), .GND(1'b0), .D0(U32_pin2[0]), .D1(U32_pin2[1]), .D2(U32_pin2[2]), .D3(U32_pin2[3]),
    .D4(U32_pin10[4]), .D5(U32_pin10[5]), .D6(U32_pin10[6]), .D7(U32_pin10[7]));
  or or_2 (SL_t, _1Y_U3, U49_pin1);
  xor xor_1 (U5__74S174_p4, Q4, nQ2);
  // _74273 U34: pin names not known; wires that end beside it: LATCH_CC, 1'b1, MD_BUS[0], MD_BUS[1], MD_BUS[2], MD_BUS[3], MD_BUS[4], MD_BUS[5], MD_BUS[6], MD_BUS[7], 1'b1, 1'b0, CC_BUS[0], CC_BUS[1], CC_BUS[2], CC_BUS[3], CC_BUS[4], CC_BUS[5], CC_BUS[6], CC_BUS[7]
  // Probe Q5 on Q5
  // Probe Q4 on Q4
  // Probe ~LCLK on nLCLK
  // Probe Q1 on Q1
  // Probe Q2 on Q2
  // Probe HCLK on HCLK
  // Probe LCLK on LCLK
  // Probe ~7MHZ on n7MHZ
  // Probe ~HCLK on nHCLK
  // Probe ~Q2 on nQ2
  // Probe ~14MHZ on n14MHZ
  // mcm4517_8bit mcm4517_8bit_1: pin names not known; wires that end beside it: nCAS, nRAS, 1'b1, MD_BUS, MD_BUS
  // _74273 U35: pin names not known; wires that end beside it: LATCH_AT, 1'b1, MD_BUS[0], MD_BUS[1], MD_BUS[2], MD_BUS[3], MD_BUS[4], MD_BUS[5], MD_BUS[6], MD_BUS[7], 1'b1, 1'b0, AT_BUS[0], AT_BUS[1], AT_BUS[2], AT_BUS[3], AT_BUS[4], AT_BUS[5], AT_BUS[6], AT7
  odd_even_splitter CC_Splitter (.BYTE_IN(CC_BUS), .ODD(CC_Splitter_odd), .EVEN(CC_Splitter_even));
  odd_even_splitter AT_Splitter (.BYTE_IN({AT7, AT_BUS}), .ODD(AT_Splitter_odd), .EVEN(AT_Splitter_even));
  mc6845 U38 (
    .VSS(1'b0), .VCC(1'b1), .nRESET(nRESET_t), .LPSTB(1'b0), .CLK(nCLK_C), .R_nW(nIOW), .E(1'b1), .RS(A0),
    .nCS(1'b1), .MA0(MA_BUS[0]), .MA1(MA_BUS[1]), .MA2(MA_BUS[2]), .MA3(MA_BUS[3]), .MA4(MA_BUS[4]),
    .MA5(MA_BUS[5]), .MA6(MA_BUS[6]), .MA7(MA_BUS[7]), .MA8(MA_BUS[8]), .MA9(MA_BUS[9]), .MA10(MA_BUS[10]),
    .MA11(MA_BUS[11]), .MA12(MA12), .DEN(DEN), .CUR(CURSOR), .RA0(RA[0]), .RA1(RA[1]), .RA2(RA[2]),
    .RA3(RA[3]), .RA4(RA[4]), .D7(pincontrol_7_p4), .D6(pincontrol_8_p4), .D5(pincontrol_5_p4),
    .D4(pincontrol_6_p4), .D3(pincontrol_3_p4), .D2(pincontrol_4_p4), .D1(pincontrol_1_p4),
    .D0(pincontrol_2_p3), .HS(HS), .VS(VS));  // open: MA13
  // _74174 U101: pin names not known; wires that end beside it: _14MHZ, 1'b1, RGBI[0], RGBI[1], RGBI[2], RGBI[3], nRESET_t, U101_p8, 1'b1, 1'b0, R, G_t, B_t, I, U101_p8, nRESET
  _74166 U7 (
    .pin1(1'b0), .pin2(AT_Splitter_even[0]), .pin3(AT_Splitter_even[1]), .pin4(AT_Splitter_even[2]),
    .pin5(AT_Splitter_even[3]), .pin6(1'b0), .pin7(CLK_DOT), .pin8(1'b0), .pin9(nCLR_SR),
    .pin10(CC_Splitter_even[0]), .pin11(CC_Splitter_even[1]), .pin12(CC_Splitter_even[2]), .pin13(C0),
    .pin14(CC_Splitter_even[3]), .pin15(SL), .pin16(1'b1));
  Seven_Seg_Hex seven_seg_hex_1 (.d({3'b000, RA[4]}), .dp(1'b0));
  Seven_Seg_Hex seven_seg_hex_2 (.d(RA[3:0]), .dp(1'b0));
  _74166 U8 (
    .pin1(1'b0), .pin2(AT_Splitter_odd[0]), .pin3(AT_Splitter_odd[1]), .pin4(AT_Splitter_odd[2]),
    .pin5(AT_Splitter_odd[3]), .pin6(1'b0), .pin7(CLK_DOT), .pin8(1'b0), .pin9(nCLR_SR),
    .pin10(CC_Splitter_odd[0]), .pin11(CC_Splitter_odd[1]), .pin12(CC_Splitter_odd[2]), .pin13(C1),
    .pin14(CC_Splitter_odd[3]), .pin15(SL), .pin16(1'b1));
  // PinControl pincontrol_1: pin names not known; wires that end beside it: pincontrol_1_p1, pincontrol_2_p1[1], 1'b0, pincontrol_1_p4
  // PinControl pincontrol_2: pin names not known; wires that end beside it: pincontrol_2_p1[0], 1'b0, pincontrol_2_p3
  // PinControl pincontrol_3: pin names not known; wires that end beside it: pincontrol_1_p1, pincontrol_2_p1[3], 1'b0, pincontrol_3_p4
  // PinControl pincontrol_4: pin names not known; wires that end beside it: pincontrol_1_p1, pincontrol_2_p1[2], 1'b0, pincontrol_4_p4
  // PinControl pincontrol_5: pin names not known; wires that end beside it: pincontrol_1_p1, pincontrol_2_p1[5], 1'b0, pincontrol_5_p4
  // PinControl pincontrol_6: pin names not known; wires that end beside it: pincontrol_1_p1, pincontrol_2_p1[4], 1'b0, pincontrol_6_p4
  // PinControl pincontrol_7: pin names not known; wires that end beside it: pincontrol_1_p1, pincontrol_2_p1[7], 1'b0, pincontrol_7_p4, pincontrol_1_p1, pincontrol_2_p1
  // PinControl pincontrol_8: pin names not known; wires that end beside it: pincontrol_1_p1, pincontrol_2_p1[6], 1'b0, pincontrol_8_p4
  // _74374 U58: pin names not known; wires that end beside it: nENCAS_CRT, nRAS, MA_BUS[7], MA_BUS[8], MA_BUS[9], MA_BUS[10], MA_BUS[11], MA12_COND, U58_p9, U58_p10, 1'b1, 1'b0, ADDR_CAS[0], ADDR_CAS[1], ADDR_CAS[2], ADDR_CAS[3], ADDR_CAS[4], ADDR_CAS[6]
  // NotConnected on U58_p9
  // NotConnected on U58_p10
  assign ADDR_CAS[5] = ~nENCAS_CRT ? nHCLK : 1'bz;  // DriverInvSel driverinvsel_1
  // RGBLED #(.Bits(2)) BG: pin names not known; wires that end beside it: BG_p1, BG_p2, BG_p3
  not not_5 (pincontrol_1_p1, nIOW);
  and and_2 (and_2_out, AT7, nBLINK_EN);
  led_driver led_driver_1 (
    .R(AT_BUS[6]), .G(AT_BUS[5]), .B(AT_BUS[4]), .I(and_2_out), .R_OUT(BG_p3), .G_OUT(BG_p2), .B_OUT(BG_p1));
  Seven_Seg_Hex seven_seg_hex_3 (.d({3'b000, MA12}), .dp(1'b0));
  // _74374 U59: pin names not known; wires that end beside it: nENRAS_CRT, nRAS, MA_BUS[0], MA_BUS[1], MA_BUS[2], MA_BUS[3], MA_BUS[4], MA_BUS[5], MA_BUS[6], U59_p10, 1'b1, 1'b0, ADDR_CAS[0], ADDR_CAS[1], ADDR_CAS[2], ADDR_CAS[3], ADDR_CAS[4], ADDR_CAS[5], ADDR_CAS[6]
  // NotConnected on U59_p10
  // Probe CASADDR on ADDR_CAS
  Seven_Seg_Hex seven_seg_hex_4 (.d(MA_BUS[11:8]), .dp(1'b0));
  Seven_Seg_Hex seven_seg_hex_5 (.d(MA_BUS[7:4]), .dp(1'b0));
  // _74153 U9__74153: pin names not known; wires that end beside it: STR, AT_BUS[2], AT_BUS[6], C1, in_22, STR, AT_BUS[1], AT_BUS[5], C0, in_23, MUX_A, MUX_B, 1'b1, 1'b0, RGBI[0], RGBI[1]
  Seven_Seg_Hex seven_seg_hex_6 (.d(MA_BUS[3:0]), .dp(1'b0));
  // Probe RASADDR on ADDR_CAS
  led_driver4 led_driver4_1 (
    .RGBI(AT_BUS[3:0]), .R_OUT(led_driver4_1_r_out), .G_OUT(led_driver4_1_g_out), .B_OUT(led_driver4_1_b_out));
  // _74153 U10__74153: pin names not known; wires that end beside it: STR, AT_BUS[0], AT_BUS[4], SEL_BLUE, in_24, STR, AT_BUS[3], and_2_out, in_20, in_25, RGBI[2]
  // _74174 U39: pin names not known; wires that end beside it: 1'b0, nRESET_t, 1'b0, 1'b0, 1'b0, 1'b0, 1'b0, 1'b0, 1'b1, 1'b0
  // RGBLED #(.Bits(2)) FG: pin names not known; wires that end beside it: led_driver4_1_r_out, led_driver4_1_g_out, led_driver4_1_b_out
  led_driver4 led_driver4_2 (
    .RGBI(RGBI), .R_OUT(led_driver4_2_r_out), .G_OUT(led_driver4_2_g_out), .B_OUT(led_driver4_2_b_out));
  mux_table MUX_Table ();  // open: o
  // RGBLED #(.Bits(2)) OUT: pin names not known; wires that end beside it: MUX_A, MUX_B, 1'b1, 1'b0, RGBI[3], led_driver4_2_r_out, led_driver4_2_g_out, led_driver4_2_b_out
  nor nor_1 (nor_1_out, nRESET_t, nRESET_t);
  _74ls393 U12 (
    .CKA(VSYNC_DLY), ._1QC(nCURSOR_BLINK), .VCC(1'b1), .GND(1'b0), ._1CLR(nor_1_out), .CKB(nCURSOR_BLINK),
    ._2QA(nBLINK), ._2CLR(nor_1_out));  // open: _1QA, _1QB, _1QD, _2QB, _2QC, _2QD
  // _74174 U40: pin names not known; wires that end beside it: 1'b0, nRESET_t, 1'b0, 1'b0, 1'b0, 1'b0, 1'b0, 1'b0, 1'b1, 1'b0
  Break #(.Cycles(1000000)) VSYNC (.brk(VSYNC_OUT_t));
  // Probe HSYNC_DLY on HSYNC_DLY
  // Probe VSYNC_DLY on VSYNC_DLY
  // Probe VSYNC_OUT' on VSYNC_OUT_t
  // Probe on CURSOR
  // Probe ~CCLK on nCLK_C
  // Probe ENRAS_CRT on nENRAS_CRT
  // Probe ENCAS_CRT on nENCAS_CRT
  // Probe CS_CROM on nCS_CROM
  // Probe SL on SL
  // Probe ~RAS on nRAS
  // Probe ~CAS on nCAS
  not not_6 (nBW_1, in_16);
  // Probe CLK_DOT on CLK_DOT
  // Probe LATCH_AT on LATCH_AT
  // Probe DOTS_CHG on DOTS_CHG
  // Probe STR on STR
  // Probe C0 on C0
  // Probe C1 on C1
  // Probe CB_U43 on CB_U43
  nor nor_2 (nor_2_out, nCURSOR_DLY, nCURSOR_BLINK);
  _7408 U13 (
    .pin1(1'b0), .pin2(1'b0), .pin4(1'b0), .pin5(1'b0), .pin7(1'b0), .pin9(1'b0), .pin10(1'b0),
    .pin11(U13_pin11), .pin12(U13_pin12), .pin13(DOTS_CHG), .pin14(1'b1));  // open: pin3, pin6, pin8
  assign MD_BUS = 1'b0 ? {8{1'b0}} : 8'bz;  // Driver driver_1
  not not_7 (nRESET_t, RESET);
  _7432 U14 (
    .pin1(AT_BLINK_GATE), .pin2(nBLINK), .pin3(U13_pin12), .pin4(U13_pin11), .pin5(nor_2_out),
    .pin6(DOTS_ALPHA), .pin7(1'b0), .pin9(1'b1), .pin10(1'b1), .pin12(1'b1), .pin13(1'b1), .pin14(1'b1));  // open: pin8, pin11
  // Probe RA0 on RA[0]
  nand nand_2 (HRES_BORDER, in_18, nDISPEN_DLY);
  _7404 U16 (
    .pin1(1'b1), .pin3(in_18), .pin4(nHRES_GFX), .pin5(in_19), .pin6(nBLINK_EN), .pin7(1'b0), .pin8(nBW_2),
    .pin9(in_16), .pin10(nGRPH), .pin11(in_15), .pin12(nHRES), .pin13(in_14), .pin14(1'b1));  // open: pin2
  _74125 U62 (
    .pin1(1'b0), .pin2(1'b0), .pin4(1'b0), .pin5(1'b0), .pin7(1'b0), .pin8(U62_pin8), .pin9(SL_t),
    .pin10(1'b0), .pin11(SL), .pin12(U62_pin8), .pin13(1'b0), .pin14(1'b1));  // open: pin3, pin6
  // _7404 U20__7404: pin names not known; wires that end beside it: CURSOR, DEN, U20__7404_p3, RESET, 1'b1, 1'b1, 1'b1, 1'b0, U20__7404_p9, nDEN, SEL_BLUE, nRESET_t
  _74175 U63 (
    .pin1(VSYNC_DLY), .pin2(U63_pin2), .pin4(1'b1), .pin5(U63_pin2), .pin7(U63_pin7), .pin8(1'b0),
    .pin9(HSYNC_OUT_t), .pin10(U63_pin10), .pin12(U63_pin7), .pin13(U63_pin10), .pin14(U63_pin14),
    .pin16(1'b1));  // open: pin3, pin6, pin11, pin15
  and and_3 (VSYNC_OUT_t, U63_pin2, U63_pin14);
  // _74174 U21__74174: pin names not known; wires that end beside it: U20__7404_p9, HCLK, nDEN, HS, 1'b1, VS, U21__74174_p7, U21__74174_p8, 1'b1, 1'b0, U21__74174_p7, U21__74174_p8, HSYNC_DLY, VSYNC_DLY, nCURSOR_DLY, nDISPEN_DLY
  nand nand_3 (nand_3_out, nDISPEN_DLY, U21__74174_p8);
  LED led_1 (.in(Q0_U64));
  LED led_2 (.in(HSYNC_OUT_t));
  LED led_3 (.in(Q2_U64));
  LED led_4 (.in(Q3_U64));
  LED led_5 (.in(Q4_U64));
  LED led_6 (.in(Q5_U64));
  LED led_7 (.in(Q6_U64));
  LED led_8 (.in(Q7_U64));
  nor nor_3 (nBLANK, VSYNC_DLY, HSYNC_DLY);
  _74164 U64 (
    .pin1(U64_pin1), .pin2(1'b1), .pin3(Q0_U64), .pin4(HSYNC_OUT_t), .pin5(Q2_U64), .pin6(Q3_U64),
    .pin7(1'b0), .pin8(LCLK), .pin9(HSYNC_DLY), .pin10(Q4_U64), .pin11(Q5_U64), .pin12(Q6_U64),
    .pin13(Q7_U64), .pin14(1'b1));
  and and_4 (nCLR_SR, in_17, nand_3_out);
  _7474 U43 (
    .pin1(HSYNC_DLY), .pin2(Q7_U64), .pin3(LCLK), .pin4(nBW_2), .pin5(U43_pin5), .pin7(1'b0), .pin8(BLUE),
    .pin9(YELLOW_BURST), .pin10(nBW_2), .pin11(_14MHZ), .pin12(n3_n58MHZ), .pin13(nBW_2), .pin14(1'b1));  // open: pin6
  not not_8 (not_8_out, Q6_U64);
  isa_slot isa_slot_1 (
    .OSC(OSC), .RESET(RESET), .SA({isa_slot_1_sa, A0}), .nIOW(nIOW), .T_C(isa_slot_1_t_c),
    .SD(isa_slot_1_sd), .IO_READY(1'b1), .IO_CK(1'b0), .PCLK_BUS(1'b0), .OSC_BUS(clk), .RESET_BUS(1'b0),
    .SD_BUS({A2, H, G, F, E, D, C, B}), .DREQ_BUS(Y), .IRQ_BUS(X), .IOREADY_BUS(Z), .IOCHK_BUS(U));  // open: VCC, GND, CLK, ALE, AEN, nIOR, nMEMR, nMEMW, nDACK
  or or_3 (CB_U43, U43_pin5, not_8_out);
  nand nand_4 (nand_4_out, Q7_U64, Q7_U64);
  xor xor_2 (U64_pin1, nand_4_out, Q3_U64);
  not not_9 (_14MHZ, OSC);
  _7474 U44 (
    .pin1(nBW_1), .pin2(YELLOW_BURST), .pin3(_14MHZ), .pin4(nBW_1), .pin5(RED), .pin6(CYAN), .pin7(1'b0),
    .pin8(GREEN), .pin9(MAGENTA), .pin10(nBW_1), .pin11(n14MHZ), .pin12(RED), .pin13(nBW_1), .pin14(1'b1));
  nor nor_4 (nEN_COLOR, VSYNC_DLY, CB_U43);
  // _7451 U22: pin names not known; wires that end beside it: U22_p1, nHRES_GFX, DOTS_ALPHA, 1'b1, in_15, nGRPH, C0, in_16, in_21, nBW_2, 1'b1, 1'b0, U22_p13, U20__7404_p3
  _7432 U23 (
    .pin1(C1), .pin2(C0), .pin3(U22_p1), .pin4(1'b0), .pin5(1'b0), .pin7(1'b0), .pin8(MUX_A), .pin9(U22_p13),
    .pin10(nDISPEN_DLY), .pin11(MUX_B), .pin12(nDISPEN_DLY), .pin13(in_15), .pin14(1'b1));  // open: pin6
  _74151 U45 (
    .pin1(CYAN), .pin2(GREEN), .pin3(BLUE), .pin4(1'b0), .pin5(CLK_COLOR), .pin7(1'b0), .pin8(1'b0),
    .pin9(U45_pin9), .pin10(U45_pin10), .pin11(B_t), .pin12(1'b1), .pin13(YELLOW_BURST), .pin14(MAGENTA),
    .pin15(RED), .pin16(1'b1));  // open: pin6
  _7486 U68 (
    .pin1(G_t), .pin2(nEN_COLOR), .pin3(U45_pin10), .pin4(R), .pin5(nEN_COLOR), .pin6(U45_pin9), .pin7(1'b0),
    .pin8(U68_pin8), .pin9(LCLK), .pin10(Q4), .pin11(nCS_CROM), .pin12(U68_pin8), .pin13(RESET), .pin14(1'b1));
  // _74244 U67: pin names not known; wires that end beside it: R, G_t, B_t, I, 1'b0, HSYNC_OUT_t, VSYNC_OUT_t, 1'b0, 1'b0, 1'b0, 1'b1, 1'b0, R_OUT, G_OUT, B_OUT, I_OUT, HSYNC_OUT, VSYNC_OUT
  edge_pulse edge_pulse_1 (.D(DEN), .CLK(n14MHZ), .PULSE(edge_pulse_1_pulse));
  Counter #(.Bits(10)) counter_1 (.en(1'b1), .C(HSYNC_OUT), .clr(VSYNC_OUT), .out(counter_1_out));  // open: ovf
  Counter #(.Bits(11)) counter_2 (.en(1'b1), .C(n14MHZ), .clr(edge_pulse_1_pulse), .out(counter_2_out));  // open: ovf
  // Probe SCANLINE on counter_1_out
  // Probe FRAME on VSYNC_OUT
  // Probe HDOT on counter_2_out
  color_shift_reg color_shift_reg_1 (
    .R(R_OUT), .G(G_OUT), .B(B_OUT), .I(I_OUT), .CLK(n14MHZ), ._0(color_shift_reg_1__0),
    ._1(color_shift_reg_1__1), ._2(color_shift_reg_1__2), ._3(color_shift_reg_1__3),
    ._4(color_shift_reg_1__4), ._5(color_shift_reg_1__5), ._6(color_shift_reg_1__6), ._7(color_shift_reg_1__7));
  dsub dsub_1 (.R(R_OUT), .G(G_OUT), .B(B_OUT), .I(I_OUT), .H(HSYNC_OUT), .V(VSYNC_OUT), .clk(n14MHZ));
  // led_driver4 led_driver4_3: pin names not known; wires that end beside it: color_shift_reg_1__7
  // RGBLED #(.Bits(2)) rgbled_1: pin names not known
  // RGBLED #(.Bits(2)) rgbled_2: pin names not known
  // led_driver4 led_driver4_4: pin names not known; wires that end beside it: color_shift_reg_1__6
  // RGBLED #(.Bits(2)) rgbled_3: pin names not known
  // led_driver4 led_driver4_5: pin names not known; wires that end beside it: color_shift_reg_1__5
  // led_driver4 led_driver4_6: pin names not known; wires that end beside it: color_shift_reg_1__4
  // RGBLED #(.Bits(2)) rgbled_4: pin names not known
  // led_driver4 led_driver4_7: pin names not known; wires that end beside it: color_shift_reg_1__3
  // RGBLED #(.Bits(2)) rgbled_5: pin names not known
  // RGBLED #(.Bits(2)) rgbled_6: pin names not known
  // led_driver4 led_driver4_8: pin names not known; wires that end beside it: color_shift_reg_1__2
  // RGBLED #(.Bits(2)) rgbled_7: pin names not known
  // led_driver4 led_driver4_9: pin names not known; wires that end beside it: color_shift_reg_1__1
  // led_driver4 led_driver4_10: pin names not known; wires that end beside it: color_shift_reg_1__0
  // RGBLED #(.Bits(2)) rgbled_8: pin names not known
  // also tied to GND on the sheet: {isa_slot_1_t_c, isa_slot_1_sd[0], isa_slot_1_sd[1], isa_slot_1_sd[2], isa_slot_1_sd[3], isa_slot_1_sd[4], isa_slot_1_sd[5], isa_slot_1_sd[6], isa_slot_1_sd[7], RESET}

  // Other names for the same wires on the sheet: MA_BUS[12] = MA12; ADDR_RAS[6:0] = ADDR_CAS; AT_BUS[7] = AT7;
  //   B_OVERSCAN = in_24; BLINK_EN = in_19; BW = in_16; G_OVERSCAN = in_23; GRPH = in_15; HRES = in_14;
  //   HRES_GFX = in_18; I_BACKGROUND = in_20; I_OVERSCAN = in_25; OSC_BUS = clk; Q1_U64 = HSYNC_OUT_t;
  //   R_OVERSCAN = in_22; SEL_COLOR = in_21; VIDEO_EN = in_17

  // Notes on the sheet:
  //   clk: Hz: 2147483647
  //   in_14: default 1
  //   in_17: default 1
  //   in_23: default 1
  //   in_24: default 1
  //   U46: RAS/CAS Enable
  //   U46 is responsible from taking inputs from U47 and U1 and synthesizing
  //   the ~ENRAS/~ENCAS signals, which are used to enable the relevant address
  //   bus drivers.
  //   It is important that only one bus driver drive the data bus at any given time.
  //   U1: RAS/CAS Sync
  //   U25: Miscellaneous NAND
  //   U29: Miscellaneous Inverters
  //   U26: Miscellaneous Inverters
  //   U30: Character Latch Timing
  //   U47: Attribute Latch Timing
  //   Unrelated signals travel here from all over the board.
  //   Only nearby connections are shown; inverting logic from elsewhere on the
  //   board will be represented by an in-line inverter component.
  //   U25C
  //   U23B
  //   RAS/CAS Generator
  //   U27: Dot and Character Clock Selector
  //   U31
  //   This XOR gate combines several of the CGA's clocks in 
  //   order to synthesize the RAS and CAS signals for RAM.
  //   U27 has the critical role of generating the Dot and
  //   Character Clocks, switching between the pairs of
  //   14Mhz / HCLK and 7Mhz / LCLK depending on the
  //    status of the HRES signal.
  //   U3D
  //   Clock Derivation
  //   Two flip-flops derive most of the CGA's clocks by division, feeding outputs back into inputs. 
  //   Each loop divides the source clock by 2.
  //   U28: Miscellaneous NAND Logic
  //   The 7410 contains 3 triple-input NAND gates.
  //   Therefore it has three separate and unrelated functions.
  //   -
  //   This NAND gates the STR signal used to enable or disable the color multiplexers.
  //   U32: Character Serializer
  //   U32 is an 8-bit parallel-in, serial-out shift register.
  //   It takes the 8-bit character glyph span from the character ROM
  //   and emits it one bit at a time at the current dot clock.
  //   Part of the text blink circuitry.
  //   Blinking must be enabled in the mode 
  //   control register, attrtibute bit 7 must be
  //   set, and no cursor can be visible.
  //   AT_BLINKGATE is gated further elsewhere.
  //   U48 & U49: MA12 control, Shift-Load Generation
  //   These two gates handle a variety of functions. 
  //   One output is MA12, which utlizes the GRPH, ~GRPH, and RA0 inputs to determine
  //   whether MA12 should be set - this creates the famous 8k offset for odd scanlines.
  //   U49 also generates the pre-Shift Load signal, SL' used for rasterization timing.
  //   U33: Character ROM
  //   The Character ROM holds fonts for both the MDA and CGA cards. 
  //   The CGA has two fonts, one of which is a "thin" font that cannot be accessed without
  //   bridging pads on the card to pull A11 low.
  //   Normally, A11 and A12 are high, which selects the last quarter of the ROM where the
  //   normal CGA font resides.
  //   The address is constructed of the first three bits of the CRTC's row scan counter, with
  //   the character code value making up the other 8.  This will produce a byte of data 
  //   representing a single scanline slice of a character glyph.
  //   U33
  //   U30C
  //   U50-U57: Video Memory
  //   U34: Character Code / Byte 0 Latch
  //   The CC latch latches the first byte of a video memory read cycle.
  //   In text mode, this is the  character code.
  //   In graphics mode, this is the first byte of pixel data, but it is still referred to
  //   as the 'CC' or character code byte.
  //   Normally comprised of 8 bit addressable DRAM modules, I've implemented VRAM
  //   as a single 8 bit module for simplicity (and speed). It otherwise works exactly the same.
  //   RAM is addressed by setting a 7 bit row address via the Row Address Strobe (RAS)
  //   followed by a 7 bit column address set via Column Address Strobe (CAS). 
  //   The ~WE pin controls whether the data presented on D is written, or if the stored data
  //   is emitted on Q.  Since we control ~RAS and ~CAS with timed enable signals, we can 
  //   tie these to the same bus.
  //   U42A
  //   U35: Attribute Byte / Byte 1  Latch
  //   The AT latch latches the first byte of a video memory read cycle.
  //   In text mode, this is the attribute byte.
  //   In graphics mode, this is the second byte byte of pixel data, but it is still referred
  //   to as the 'AT' or attribute byte.
  //   U7 & U8: Color Serializers
  //   These two chips serialize out pixel data for medium-resolution graphics mode.
  //   Their outputs are C0 and C1 which represent a pair of bits that make up a 2bpp pixel.
  //   C0 is the even bit, and C1 is the odd bit.
  //   U101: Color / Reset Latch
  //   This flip-flop latches the RGBI output of the color multiplexers
  //   at the native 14MHz clock. 
  //   Its secondary role is to produce the ~RESET signal from the 
  //   ~RESET' input, delayed by one clock.
  //   U38: 6845 Cathode Ray Tube Controller
  //   The 6845 CRTC is a somewhat complex LSI device and a full analysis of its operation is a bit out of scope.
  //   The 6845 here is implemented in Verilog - it is a simple implementation without many of the 6845's tricker edge cases.
  //   For the definitive description of the 6845's operation, see Logon System's "CRTC Compendium"
  //   U58 & U59: RAM Address Drivers
  //   The CRTC is responsible for producing character cell and row scan
  //   addresses based on the geometry programmed into its registers.
  //   It is clocked at the "character clock" which is adjusted based on video
  //   mode.
  //   U58 and U59 latch the CAS and RAS addresses, respectively, on
  //   every rising edge of ~RAS. 
  //   For the CAS address, additional logic drives bits 12 and 13 of the
  //   memory address. In graphics mode, bit 13 is driven by RA0 of the 
  //   CRTC's row counter to produce an odd/even scanline interleaved
  //   offset of 8k.
  //   In text mode, bit 13 of the memory address is driven MA12.
  //   In all modes, bit 12 of the memory address is driven by ~HCLK.
  //   U9 & U10: Color Multiplexers
  //   These two chips are where the primary color generation happens.
  //   The MUX_A and MUX_B inputs form two bits that select four of 16 inputs that create the RGBI pixel.
  //   A high STR or "Strobe" input forces all the outputs of the multiplexers low, generating black.
  //   U31C
  //   U39: Color Control Register
  //   The Color Control (CC) register provides various color signals.
  //   The complete 4 bits of the overscan/background color is defined here.
  //   The intensity and blue bits of the 'palette' are also selected.
  //   Legend
  //   Signals with ~OVERBARS indicate that this signal is active-low, ie, 
  //   it is logically true when the logic level is 0.
  //   Therefore GRPH may indicate "in graphics mode" and ~GRPH 
  //   "not in graphics mode"
  //   A trailing tick ' on a signal means that this signal eventually 
  //   generates the final undecorated signal after additional logic or 
  //   delays.
  //   Small triangles are tunnels - these make "wireless" connections 
  //   to all other tunnels of the same name. This just simplifies the diagram.
  //   CGA Palette
  //   The IBM Color Graphics Adapter
  //   U12: Blink Generator
  //   Although the 6845 provides cursor blinking, the CGA produces its own
  //   blink timings for the cursor and  for blinking text, by ticking this 4-bit 
  //   counter.
  //   It is synchronized via ~RESET' so that normally it is in sync with the 
  //   6845's blinking.  The net effect is unnoticeable in normal operation
  //   except for the fact that you cannot disable blinking via the 6845.
  //   This logic does not, however, account for the 6845's "slow blink" mode,
  //   and if set the cursor will blink at the combination of both blink signals.
  //   The text ~BLINK signal ends up half the rate of ~CURSOR_BLINK.
  //   U65D
  //   U40: Mode Control Register
  //   The CGA's mode control register directly controls many high level signals.
  //   Some of these signals are not indended to be active at the same time,
  //   which can lead to interesting and undocumented effects.
  //   HRES: Enables timings for high resolution text mode
  //   GRPH: Enables graphics rasterization
  //   BW: Disables the NTSC color burst, selects alternate palette
  //   VE: Disables display within the active display area (overscan still drawn)
  //   HRES_GFX: Enable the high res graphics mode
  //   BLINK_EN: Interpret attribute bit 7 as 'blink' for text
  //   Breakpoints
  //   Probes
  //   U13 & U14: Character Generator Dot Gate
  //   This logic determines whether the dots produced by the  character generator (DOTS_CHG)
  //   become visible dots (DOTS_ALPHA) or are suppressed due to blinking.
  //   U29D
  //   U49D
  //   U15: Miscellaneous NAND
  //   HRES_BORDER = 
  //   NOT ( In high res graphics OR in the display area)
  //   U65B
  //   U16: Signal Inverter
  //   This 7404 Hex Inverter produces the complement of several control signals.
  //   U41: Misc AND Logic
  //   U62: Signal Buffer
  //   ISA Slot Connector
  //   Simple AND gates are shown inline to simplify  the diagram.
  //   Passing signals through this buffer can introduce
  //   a propagation delay which may be useful for timing.
  //   Here the Shift-Load singal SL' becomes the final SL.
  //   U20 & U21: Miscellaneous Signal Logic
  //   This pair of chips, a hex inverter (U20) and a D-type flip-flop (U21) perform minor signal logic.
  //   U20 directly produces the ~RESET', ~DEN, and SEL_BLUE signals from their complements.
  //   HS,VS enter the flip flop directly, while CURSOR and DEN pass through both the inverter and the flip flop.
  //   The flilp flop is clocked via HCLK and produces complementary signals that are delayed, and thus have the 'DLY' suffix.
  //   ~HSYNC_DLY and ~VSYNC_DLY are delayed by one HCLK.
  //   ~CURSOR and ~DEN are fed back into the flip flop, and thus are delayed by two HCLKs. 
  //   Additional logic stages follow, shown here as simplified gates for simplicity of wiring:
  //   • The ~CLR_SR signal is derived from ~DEN, ~DEN_DLY, and VIDEO_EN.  This clears the shift registers when not in the active display area.
  //   • The ~BLANK signal is derived from NOR of HSYNC_DLY and VSYNC_DLY as either hsync or vsync is considered the "blanking period"
  //   U42: Misc XOR Logic
  //   Simple XOR gates are shown inline to simplify  the diagram.
  //   U63: VSYNC Clock
  //   This flip flop delays the final VSYNC signal sent to the monitor
  //   until the next HSYNC, and adjusts it so that it is three scanlines 
  //   in length.
  //   U41C
  //   U43: Burst Timing & Blue Color Clock
  //   The left half of U43 is dedicated to generating NTSC color burst
  //   signal timings.
  //   The right half is the first stage of the composite color clock
  //   generator, generating the BLUE and YELLOW_BURST clocks.
  //   Both outputs are disabled by the ~BW_2 signal.
  //   U64: HSYNC Clock
  //   This binary counter produces the final HSYNC signal, delaying
  //   it until the next LCLK.
  //   It emits signals to U43 above to generate the color burst 
  //   timing.  Note that in 80 column mode, we never reach Q6
  //   and so the color burst is effectively disabled.
  //   U15A
  //   U13A
  //   U20E
  //   The CGA's 14MHz clock signal is the inverted
  //   14MHz clock from the ISA bus.
  //   U14D
  //   U15B
  //   U26A
  //   U22 & U23: MUX Control
  //   U44: Color Clock Generator
  //   U65: Misc NOR Logic
  //   U42C
  //   These chips perform two main functions. Firstly, they produce the MUX_A and MUX_B signals. 
  //   MUX_A and MUX_B are inputs to the color multiplexer and  determine the color source used for rasterization.
  //   (See U9 & U10)
  //   U22 also produces the ~SEL_BLUE signal which is used by the color multiplexers to control the blue channel.
  //   U23B is also used as an OR gate unrelated to MUX logic, which is not shown here.
  //   MUX Inputs
  //   SEL_BLUE Inputs
  //   Continuing from U43, U44 produces the RED, CYAN, MAGENTA
  //   and GREEN color clocks.
  //   Its outputs are disabled by the ~BW_1 signal.
  //   Simple NOR gates are shown inline to simplify  the diagram.
  //   R & G signals are disabled in the absence of color burst 
  //   or during VSYNC.
  //   U45: Color Multiplexer
  //   U45 selects from 8 color clock sources based on the 3-bit input
  //   of R, G and B.  
  //   0 is tied low for black, and 7 is tied high for white.
  //   The output of the color multiplexer is an input into the analog 
  //   composite circuitry, which we cannot simulate here.
  //   U66
  //   U68: XOR Logic
  //   The left side of U68 gates the R and G inputs to the color 
  //   multiplexer U45.
  //   The right side of U68 produces the chip select for the character
  //   ROM via XOR of the Q4 and LCLK clocks.
  //   U67: RGBI Output Buffer
  //   RGBI DE-9 Output
endmodule
