// Digital circuit clr_sr.dig as structural Verilog
module clr_sr (
  input  nDEN_DLY,
  input  nDEN,
  input  VIDEO_EN,
  output nCLR_SR
);

  wire nand_1_out, not_1_out;

  nand nand_1 (nand_1_out, nDEN_DLY, nDEN);
  and and_1 (nCLR_SR, VIDEO_EN, nand_1_out);
  not not_1 (not_1_out, nCLR_SR);
  LED led_1 (.in(not_1_out));

  // Notes on the sheet:
  //   VIDEO_EN: default 1
  //   U15A
  //   U13A
endmodule
