// Digital circuit color_shift_reg.dig as structural Verilog
module color_shift_reg (
  input  R,
  input  G,
  input  B,
  input  I,
  input  CLK,
  output [3:0] _0,
  output [3:0] _1,
  output [3:0] _2,
  output [3:0] _3,
  output [3:0] _4,
  output [3:0] _5,
  output [3:0] _6,
  output [3:0] _7
);

  D_FF #(.Bits(4)) d_ff_1 (.D({I, B, G, R}), .C(CLK), .Q(_0));  // open: nQ
  D_FF #(.Bits(4)) d_ff_2 (.D(_0), .C(CLK), .Q(_1));  // open: nQ
  D_FF #(.Bits(4)) d_ff_3 (.D(_1), .C(CLK), .Q(_2));  // open: nQ
  D_FF #(.Bits(4)) d_ff_4 (.D(_2), .C(CLK), .Q(_3));  // open: nQ
  D_FF #(.Bits(4)) d_ff_5 (.D(_3), .C(CLK), .Q(_4));  // open: nQ
  D_FF #(.Bits(4)) d_ff_6 (.D(_4), .C(CLK), .Q(_5));  // open: nQ
  D_FF #(.Bits(4)) d_ff_7 (.D(_5), .C(CLK), .Q(_6));  // open: nQ
  D_FF #(.Bits(4)) d_ff_8 (.D(_6), .C(CLK), .Q(_7));  // open: nQ
endmodule
