// Digital circuit crtc_tester.dig as structural Verilog
module crtc_tester (
  input  in_1,
  input  in_2,
  input  in_3,
  input  in_4,
  input  in_5,
  input  in_6,
  input  in_7,
  input  in_8,
  input  in_9,
  input  in_10,
  input  in_11,
  input  in_12,
  input  in_13,
  input  in_14,
  input  _14MHz,
  input  nRESET,
  output HCLK,
  output n7MHz,
  output Q1,
  output n3_n58MHz
);

  wire _74174_1_pin2, _74174_1_pin3, _74174_1_pin5, _74174_1_pin7, _74174_1_pin10, _74174_1_pin12,
       _74174_1_pin15, _74174_2_pin5, _74174_2_pin6, _74174_2_pin10, _74174_2_pin13, _74174_2_pin15,
       mc6845_1_cur, mc6845_1_hs, mc6845_1_ma3, mc6845_1_ma4, mc6845_1_ma5, mc6845_1_ma6, mc6845_1_ma7,
       mc6845_1_ma8, mc6845_1_ma9, mc6845_1_ma10, mc6845_1_ma11, mc6845_1_ma12, mc6845_1_ma13, mc6845_1_ra0,
       mc6845_1_ra1, mc6845_1_ra2, mc6845_1_ra3, mc6845_1_ra4, mc6845_1_vs, not_4_out, not_5_out;
  wire [2:0] and_1_out, mc6845_1_ma2;
  wire [2:2] mc6845_1_den;
  wire [15:0] SL_out;
  wire [31:0] FRAME_out;

  _74174 _74174_1 (
    .pin1(nRESET), .pin2(_74174_1_pin2), .pin3(_74174_1_pin3), .pin4(_74174_1_pin2), .pin5(_74174_1_pin5),
    .pin6(_74174_1_pin5), .pin7(_74174_1_pin7), .pin8(1'b0), .pin9(_14MHz), .pin10(_74174_1_pin10),
    .pin11(_74174_1_pin7), .pin12(_74174_1_pin12), .pin13(_74174_1_pin10), .pin14(_74174_1_pin12),
    .pin15(_74174_1_pin15), .pin16(1'b1));
  _74174 _74174_2 (
    .pin1(nRESET), .pin2(Q1), .pin3(_74174_1_pin15), .pin4(Q1), .pin5(_74174_2_pin5), .pin6(_74174_2_pin6),
    .pin7(HCLK), .pin8(1'b0), .pin9(_14MHz), .pin10(_74174_2_pin10), .pin11(n7MHz), .pin12(n3_n58MHz),
    .pin13(_74174_2_pin13), .pin14(n3_n58MHz), .pin15(_74174_2_pin15), .pin16(1'b1));
  not not_1 (_74174_2_pin13, _74174_2_pin15);
  not not_2 (n7MHz, _74174_2_pin10);
  not not_3 (_74174_1_pin3, _74174_2_pin5);
  xor xor_1 (_74174_2_pin6, _74174_1_pin7, _74174_1_pin3);
  LED led_1 (.in(mc6845_1_ma2[0]));
  LED led_2 (.in(mc6845_1_ma2[1]));
  LED led_3 (.in(mc6845_1_ma2[2]));
  LED led_4 (.in(mc6845_1_ma3));
  LED led_5 (.in(mc6845_1_ma4));
  LED led_6 (.in(mc6845_1_ma5));
  LED led_7 (.in(mc6845_1_ma6));
  LED led_8 (.in(mc6845_1_ma7));
  LED led_9 (.in(mc6845_1_ma8));
  LED led_10 (.in(mc6845_1_ma9));
  LED led_11 (.in(mc6845_1_ma10));
  LED led_12 (.in(mc6845_1_ma11));
  LED led_13 (.in(mc6845_1_ma12));
  LED led_14 (.in(mc6845_1_ma13));
  LED led_15 (.in(mc6845_1_den[2]));
  LED led_16 (.in(mc6845_1_cur));
  mc6845 mc6845_1 (
    .VSS(1'b1), .VCC(1'b0), .nRESET(in_14), .LPSTB(in_13), .CLK(HCLK), .R_nW(in_12), .E(in_11), .RS(in_10),
    .nCS(in_9), .MA0(mc6845_1_ma2[0]), .MA1(mc6845_1_ma2[1]), .MA2(mc6845_1_ma2[2]), .MA3(mc6845_1_ma3),
    .MA4(mc6845_1_ma4), .MA5(mc6845_1_ma5), .MA6(mc6845_1_ma6), .MA7(mc6845_1_ma7), .MA8(mc6845_1_ma8),
    .MA9(mc6845_1_ma9), .MA10(mc6845_1_ma10), .MA11(mc6845_1_ma11), .MA12(mc6845_1_ma12),
    .MA13(mc6845_1_ma13), .DEN(mc6845_1_den[2]), .CUR(mc6845_1_cur), .RA0(mc6845_1_ra0), .RA1(mc6845_1_ra1),
    .RA2(mc6845_1_ra2), .RA3(mc6845_1_ra3), .RA4(mc6845_1_ra4), .D7(in_8), .D6(in_7), .D5(in_6), .D4(in_5),
    .D3(in_4), .D2(in_3), .D1(in_2), .D0(in_1), .HS(mc6845_1_hs), .VS(mc6845_1_vs));
  LED led_17 (.in(mc6845_1_ra0));
  LED led_18 (.in(mc6845_1_ra1));
  LED led_19 (.in(mc6845_1_ra2));
  LED led_20 (.in(mc6845_1_ra3));
  LED led_21 (.in(mc6845_1_ra4));
  LED led_22 (.in(mc6845_1_vs));
  LED led_23 (.in(mc6845_1_hs));
  not not_4 (not_4_out, mc6845_1_hs);
  not not_5 (not_5_out, mc6845_1_vs);
  dsub dsub_1 (
    .R(and_1_out[0]), .G(and_1_out[1]), .B(and_1_out[2]), .I(mc6845_1_ma4), .H(not_4_out), .V(not_5_out),
    .clk(_14MHz));
  Counter #(.Bits(32)) FRAME (.en(1'b1), .C(mc6845_1_vs), .clr(1'b0), .out(FRAME_out));  // open: ovf
  Counter #(.Bits(16)) SL (.en(1'b1), .C(mc6845_1_hs), .clr(1'b0), .out(SL_out));  // open: ovf
  assign and_1_out = mc6845_1_ma2 & {3{mc6845_1_den[2]}};  // And and_1, 3 bits wide
  // Probe on FRAME_out
  // Probe on SL_out

  // Notes on the sheet:
  //   in_14: default 1
  //   _14MHz: Hz: 2147483647
  //   nRESET: default 1
endmodule
