// Digital circuit dsub.dig as structural Verilog
module dsub (
  input  R,
  input  G,
  input  B,
  input  I,
  input  H,
  input  V,
  input  clk
);

  wire [1:0] u_cga_to_rgb_b_out, u_cga_to_rgb_g_out, u_cga_to_rgb_r_out;

  cga_to_rgb #(.applicationType("IVERILOG"), .CodeFile("F:\\digital\\projects\\cga\\cga_to_rgb.v")) u_cga_to_rgb (
    .r_in(R), .g_in(G), .b_in(B), .i_in(I), .r_out(u_cga_to_rgb_r_out), .g_out(u_cga_to_rgb_g_out),
    .b_out(u_cga_to_rgb_b_out));
  VGA vga_1 (.R(u_cga_to_rgb_r_out), .G(u_cga_to_rgb_g_out), .B(u_cga_to_rgb_b_out), .H(H), .V(V), .C(clk));

  // Notes on the sheet:
  //   R: pin 3
  //   G: pin 4
  //   B: pin 5
  //   I: pin 6
  //   H: pin 8
  //   V: pin 9
endmodule
