// Digital circuit edge_pulse.dig as structural Verilog
// This circuit produces a pulse of one clock length on a rising edge of the input D.
module edge_pulse (
  input  D,
  input  CLK,
  output PULSE
);

  wire d_ff_1_q, not_1_out;

  D_FF d_ff_1 (.D(D), .C(CLK), .Q(d_ff_1_q));  // open: nQ
  not not_1 (not_1_out, d_ff_1_q);
  and and_1 (PULSE, D, not_1_out);
endmodule
