// Digital circuit isa_slot.dig as structural Verilog
module isa_slot (
  input  PCLK_BUS,
  input  OSC_BUS,
  input  RESET_BUS,
  input  [7:0] SD_BUS,
  input  IO_CK,
  input  IO_READY,
  output RESET,
  output VCC,
  output nMEMW,
  output CLK,
  output OSC,
  output [19:0] SA,
  output ALE,
  output AEN,
  output nIOR,
  output nIOW,
  output nMEMR,
  output [2:0] nDACK,
  output T_C,
  output IOREADY_BUS,
  output [7:0] SD,
  output GND,
  output IOCHK_BUS,
  output [5:0] IRQ_BUS,
  output [2:0] DREQ_BUS
);

  isa_8bit_slot #(.applicationType("IVERILOG"), .CodeFile("F:\\digital\\projects\\cga\\isa.v")) u_isa_8bit_slot (
    .bus_vcc(1'b1), .bus_gnd(1'b0), .bus_clk(PCLK_BUS), .bus_osc(OSC_BUS), .bus_reset_drv(RESET_BUS),
    .bus_sa({20{1'b0}}), .bus_ale(1'b0), .bus_aen(1'b0), .bus_ior_n(1'b1), .bus_iow_n(1'b1),
    .bus_memr_n(1'b1), .bus_memw_n(1'b1), .bus_dack_n(3'b001), .bus_tc(1'b0), .card_io_ch_ck_n(IO_CK),
    .card_io_ch_rdy(IO_READY), .card_irq({6{1'b0}}), .card_drq(3'b000), .card_vcc(VCC), .card_gnd(GND),
    .card_clk(CLK), .card_osc(OSC), .card_reset_drv(RESET), .card_sa(SA), .card_ale(ALE), .card_aen(AEN),
    .card_ior_n(nIOR), .card_iow_n(nIOW), .card_memr_n(nMEMR), .card_memw_n(nMEMW), .card_dack_n(nDACK),
    .card_tc(T_C), .bus_io_ch_ck_n(IOCHK_BUS), .bus_io_ch_rdy(IOREADY_BUS), .bus_irq(IRQ_BUS),
    .bus_drq(DREQ_BUS), .bus_sd(SD_BUS), .card_sd(SD));
endmodule
