// Digital circuit latch_test.dig as structural Verilog
module latch_test (
  input  in_1,
  input  clk
);

  wire U58_p13, U58_p14, U58_p15, U58_p16, U58_p17, U58_p18, U58_p19, U58_p20;

  // _74374 U58: pin names not known; wires that end beside it: clk, in_1, 1'b0, 1'b0, 1'b0, 1'b0, 1'b0, 1'b0, 1'b0, 1'b0, 1'b1, 1'b0, U58_p13, U58_p14, U58_p15, U58_p16, U58_p17, U58_p18, U58_p19, U58_p20
  LED led_1 (.in(U58_p13));
  LED led_2 (.in(U58_p14));
  LED led_3 (.in(U58_p15));
  LED led_4 (.in(U58_p16));
  LED led_5 (.in(U58_p17));
  LED led_6 (.in(U58_p18));
  LED led_7 (.in(U58_p19));
  LED led_8 (.in(U58_p20));

  // Notes on the sheet:
  //   clk: Hz: 100
endmodule
