// Digital circuit led_driver.dig as structural Verilog
module led_driver (
  input  R,
  input  G,
  input  B,
  input  I,
  output [1:0] R_OUT,
  output [1:0] G_OUT,
  output [1:0] B_OUT
);


  assign B_OUT = {B, I};
  assign G_OUT = {G, I};
  assign R_OUT = {R, I};
endmodule
