// Digital circuit led_driver4.dig as structural Verilog
module led_driver4 (
  input  [3:0] RGBI,
  output [1:0] R_OUT,
  output [1:0] G_OUT,
  output [1:0] B_OUT
);


  assign B_OUT = {RGBI[2], RGBI[3]};
  assign G_OUT = {RGBI[1], RGBI[3]};
  assign R_OUT = {RGBI[0], RGBI[3]};
endmodule
