// Digital circuit main.dig as structural Verilog
module main (
  input  clk,
  input  B,
  input  C,
  input  D,
  input  E,
  input  F,
  input  G,
  input  H,
  input  A2,
  input  clk_2,
  input  in_15,
  input  in_16,
  input  in_17,
  input  in_18,
  input  in_19,
  input  in_20,
  input  in_21,
  input  in_22,
  input  in_23,
  input  in_24,
  input  in_25,
  input  in_26,
  output [2:0] Y,
  output [5:0] X,
  output Z,
  output U
);

  wire _1Y, _14MHZ, A0, and_2_out, and_3_out, and_4_out, AT7, AT_BLINK_GATE, B_t, C0, C1, CAS_CC, CHGDOTS,
       CS_CROM, CURSOR, DEN, DOTCLOCK, DOTS_ALPHA, G_t, HCLK, HRES_BORDER, HS, HSYNC_DLY, I, isa_slot_1_t_c,
       LATCH_AT, LATCH_CC, LCLK, MA12, MA12_COND, MUX_A, MUX_B, n3_n58MHZ, n7MHZ, n14MHZ, nand_3_out, nBLINK,
       nBLINK_EN, nBW_2, nCAS, nCCLK, nCLR_SR, nCURSOR_BLINK, nCURSOR_DLY, nDEN, nDISPEN_DLY, nENCAS_CPU,
       nENCAS_CRT, nENRAS_CPU, nENRAS_CRT, nGRPH, nHCLK, nHRES, nHRES_GFX, nIOW, nLCLK, nor_1_out, nor_2_out,
       not_1_out, not_3_out, nQ2, nRAS, nRESET, nRESET_t, nSYNC, or_1_out, OSC, pincontrol_1_p1,
       pincontrol_1_p4, pincontrol_2_p3, pincontrol_3_p4, pincontrol_4_p4, pincontrol_5_p4, pincontrol_6_p4,
       pincontrol_7_p4, pincontrol_8_p4, Q1, Q2, Q2_U4, Q4, Q5, R, RAS, RESET, SEL_BLUE, SL, SL_t, STR,
       U1_p15, U3_p13, U4__74LS174_p6, U4__74LS174_p16, U5__74S174_p4, U5__74S174_p7, U5__74S174_p14,
       U5__74S174_p16, U13_pin11, U13_pin12, U20_p3, U20_p9, U21_p7, U21_p8, U22_p1, U22_p13, U25_pin1,
       U25_pin3, U25_pin13, U26_pin8, U26_pin9, U30_pin6, U46_pin1, U46_pin2, U46_pin9, U46_pin13,
       U48_2_pin8, U49_pin1, U58_p9, U58_p10, U59_p10, U62_pin8, U67_p13, U67_p14, U67_p15, U67_p16, U67_p17,
       U67_p18, U68_pin8, U101_p8, VS, VSYNC_DLY;
  wire [3:0] AT_Splitter_even, AT_Splitter_odd, CC_Splitter_even, CC_Splitter_odd, RGBI;
  wire [4:0] RA;
  wire [6:0] ADDR_CAS, AT_BUS, d_ff_1_q, d_ff_2_q;
  wire [7:0] CC_BUS, isa_slot_1_sd, MD_BUS, pincontrol_2_p1, U32_pin2;
  wire [9:0] SCANLINE_out;
  wire [11:0] MA_BUS;
  wire [19:1] isa_slot_1_sa;

  not not_1 (not_1_out, Q5);
  _7400 U25 (
    .pin1(U25_pin1), .pin2(DOTCLOCK), .pin3(U25_pin3), .pin4(1'b0), .pin5(1'b0), .pin7(1'b0), .pin9(1'b1),
    .pin10(1'b1), .pin11(U25_pin1), .pin12(U25_pin3), .pin13(U25_pin13), .pin14(1'b1));  // open: pin6, pin8
  _7400 U46 (
    .pin1(U46_pin1), .pin2(U46_pin2), .pin3(nENRAS_CPU), .pin4(U46_pin1), .pin5(U46_pin2), .pin6(nENCAS_CPU),
    .pin7(1'b0), .pin8(nENRAS_CRT), .pin9(U46_pin9), .pin10(U46_pin2), .pin11(nENCAS_CRT), .pin12(U46_pin9),
    .pin13(U46_pin13), .pin14(1'b1));
  // _74112 U1: pin names not known; wires that end beside it: 1'b1, RAS, _14MHZ, nRAS, 1'b1, 1'b1, Q5, _14MHZ, not_1_out, 1'b1, 1'b1, 1'b0, U46_pin13, U46_pin2, U1_p15
  not not_2 (U46_pin1, U46_pin9);
  nand nand_1 (LATCH_CC, U30_pin6, CAS_CC);
  _7404 U26 (
    .pin1(1'b1), .pin3(1'b1), .pin5(1'b1), .pin7(1'b0), .pin8(U26_pin8), .pin9(U26_pin9), .pin10(U25_pin13),
    .pin11(DOTCLOCK), .pin12(_14MHZ), .pin13(OSC), .pin14(1'b1));  // open: pin2, pin4, pin6
  _7432 U30 (
    .pin1(1'b0), .pin2(1'b0), .pin4(nCCLK), .pin5(in_15), .pin6(U30_pin6), .pin7(1'b0), .pin9(1'b0),
    .pin10(1'b0), .pin12(1'b0), .pin13(1'b0), .pin14(1'b1));  // open: pin3, pin8, pin11
  _7451 U47 (
    .pin1(in_16), .pin2(in_16), .pin3(in_15), .pin4(Q1), .pin5(nHRES), .pin6(U46_pin9), .pin7(1'b0),
    .pin8(LATCH_AT), .pin9(nGRPH), .pin10(1'b1), .pin11(nCCLK), .pin12(nQ2), .pin13(1'b1), .pin14(1'b1));
  or or_1 (or_1_out, U26_pin8, nHRES_GFX);
  _7451 U48 (
    .pin1(1'b1), .pin2(C0), .pin3(U25_pin3), .pin4(C1), .pin5(U25_pin1), .pin6(U26_pin9), .pin7(1'b0),
    .pin9(1'b1), .pin10(1'b1), .pin11(1'b1), .pin12(1'b1), .pin13(1'b1), .pin14(1'b1));  // open: pin8
  // _7486 U3: pin names not known; wires that end beside it: Q2, nLCLK, Q1, nLCLK, nLCLK, U1_p15, Q2_U4, Q4, 1'b1, 1'b0, _1Y, RAS, U3_p13, CAS_CC
  _7451 U27 (
    .pin1(n7MHZ), .pin2(in_15), .pin3(HCLK), .pin4(nHRES), .pin5(LCLK), .pin6(nCCLK), .pin7(1'b0),
    .pin8(DOTCLOCK), .pin9(in_15), .pin10(1'b1), .pin11(n14MHZ), .pin12(nHRES), .pin13(1'b1), .pin14(1'b1));
  not not_3 (not_3_out, CAS_CC);
  not not_4 (nRAS, RAS);
  and and_1 (nCAS, U3_p13, not_3_out);
  // Probe on nCCLK
  // _74174 U4__74LS174: pin names not known; wires that end beside it: nQ2, _14MHZ, nLCLK, Q2_U4, nRESET_t, U4__74LS174_p6, Q4, Q5, 1'b1, 1'b0, nLCLK, Q2_U4, U4__74LS174_p6, Q4, Q5, U4__74LS174_p16
  _7410 U28 (
    .pin1(HRES_BORDER), .pin2(nSYNC), .pin3(1'b0), .pin4(1'b0), .pin5(1'b0), .pin7(1'b0),
    .pin8(AT_BLINK_GATE), .pin9(nCURSOR_DLY), .pin10(in_20), .pin11(AT7), .pin12(STR), .pin13(or_1_out),
    .pin14(1'b1));  // open: pin6
  _74166 U32 (
    .pin1(1'b0), .pin2(U32_pin2[0]), .pin3(U32_pin2[1]), .pin4(U32_pin2[2]), .pin5(U32_pin2[3]), .pin6(1'b0),
    .pin7(DOTCLOCK), .pin8(1'b0), .pin9(nCLR_SR), .pin10(U32_pin2[4]), .pin11(U32_pin2[5]),
    .pin12(U32_pin2[6]), .pin13(CHGDOTS), .pin14(U32_pin2[7]), .pin15(SL), .pin16(1'b1));
  _7451 U48_2 (
    .pin1(RA[0]), .pin2(1'b0), .pin3(1'b0), .pin4(1'b0), .pin5(1'b0), .pin7(1'b0), .pin8(U48_2_pin8),
    .pin9(MA12), .pin10(1'b1), .pin11(nGRPH), .pin12(in_16), .pin13(1'b1), .pin14(1'b1));  // open: pin6
  // _74174 U5__74S174: pin names not known; wires that end beside it: U4__74LS174_p16, _14MHZ, Q1, U5__74S174_p4, nRESET_t, n7MHZ, U5__74S174_p7, nQ2, 1'b1, 1'b0, Q1, Q2, HCLK, U5__74S174_p14, n3_n58MHZ, U5__74S174_p16
  _7402 U49 (
    .pin1(U49_pin1), .pin2(Q2_U4), .pin3(in_15), .pin5(1'b0), .pin6(1'b0), .pin7(1'b0), .pin8(U48_2_pin8),
    .pin9(U48_2_pin8), .pin10(MA12_COND), .pin11(1'b0), .pin12(1'b0), .pin14(1'b1));  // open: pin4, pin13
  // _7404 U6__7404: pin names not known; wires that end beside it: nLCLK, U5__74S174_p16, U5__74S174_p14, HCLK, Q2, _14MHZ, 1'b1, 1'b0, LCLK, U5__74S174_p7, n7MHZ, nHCLK, nQ2, n14MHZ
  mk36000 U33 (
    .A0(RA[0]), .A1(RA[1]), .nCE(CS_CROM), .A2(RA[2]), .A3(CC_BUS[0]), .A4(CC_BUS[1]), .A5(CC_BUS[2]),
    .A6(CC_BUS[3]), .A7(CC_BUS[4]), .A8(CC_BUS[5]), .A9(CC_BUS[6]), .A10(CC_BUS[7]), .A11(1'b1), .A12(1'b1),
    .VCC(1'b1), .GND(1'b0), .D0(U32_pin2[0]), .D1(U32_pin2[1]), .D2(U32_pin2[2]), .D3(U32_pin2[3]),
    .D4(U32_pin2[4]), .D5(U32_pin2[5]), .D6(U32_pin2[6]), .D7(U32_pin2[7]));
  // Probe on MA12_COND
  or or_2 (SL_t, _1Y, U49_pin1);
  xor xor_1 (U5__74S174_p4, Q4, nQ2);
  // _74273 U34: pin names not known; wires that end beside it: LATCH_CC, 1'b1, MD_BUS[0], MD_BUS[1], MD_BUS[2], MD_BUS[3], MD_BUS[4], MD_BUS[5], MD_BUS[6], MD_BUS[7], 1'b1, 1'b0, CC_BUS[0], CC_BUS[1], CC_BUS[2], CC_BUS[3], CC_BUS[4], CC_BUS[5], CC_BUS[6], CC_BUS[7]
  // Probe Q5 on Q5
  // Probe Q4 on Q4
  // Probe ~LCLK on nLCLK
  // Probe Q1 on Q1
  // Probe Q2 on Q2
  // Probe HCLK on HCLK
  // Probe LCLK on LCLK
  // Probe ~7MHZ on n7MHZ
  // Probe ~HCLK on nHCLK
  // Probe ~Q2 on nQ2
  // Probe ~14MHZ on n14MHZ
  // mcm4517_8bit mcm4517_8bit_1: pin names not known; wires that end beside it: nCAS, nRAS, 1'b1, MD_BUS, MD_BUS
  // _74273 U35: pin names not known; wires that end beside it: LATCH_AT, 1'b1, MD_BUS[0], MD_BUS[1], MD_BUS[2], MD_BUS[3], MD_BUS[4], MD_BUS[5], MD_BUS[6], MD_BUS[7], 1'b1, 1'b0, AT_BUS[0], AT_BUS[1], AT_BUS[2], AT_BUS[3], AT_BUS[4], AT_BUS[5], AT_BUS[6], AT7
  odd_even_splitter CC_Splitter (.BYTE_IN(CC_BUS), .ODD(CC_Splitter_odd), .EVEN(CC_Splitter_even));
  odd_even_splitter AT_Splitter (.BYTE_IN({AT7, AT_BUS}), .ODD(AT_Splitter_odd), .EVEN(AT_Splitter_even));
  mc6845 U38 (
    .VSS(1'b0), .VCC(1'b1), .nRESET(nRESET_t), .LPSTB(1'b0), .CLK(nCCLK), .R_nW(nIOW), .E(1'b1), .RS(A0),
    .nCS(1'b1), .MA0(MA_BUS[0]), .MA1(MA_BUS[1]), .MA2(MA_BUS[2]), .MA3(MA_BUS[3]), .MA4(MA_BUS[4]),
    .MA5(MA_BUS[5]), .MA6(MA_BUS[6]), .MA7(MA_BUS[7]), .MA8(MA_BUS[8]), .MA9(MA_BUS[9]), .MA10(MA_BUS[10]),
    .MA11(MA_BUS[11]), .MA12(MA12), .DEN(DEN), .CUR(CURSOR), .RA0(RA[0]), .RA1(RA[1]), .RA2(RA[2]),
    .RA3(RA[3]), .RA4(RA[4]), .D7(pincontrol_7_p4), .D6(pincontrol_8_p4), .D5(pincontrol_5_p4),
    .D4(pincontrol_6_p4), .D3(pincontrol_3_p4), .D2(pincontrol_4_p4), .D1(pincontrol_1_p4),
    .D0(pincontrol_2_p3), .HS(HS), .VS(VS));  // open: MA13
  _74166 U7 (
    .pin1(1'b0), .pin2(AT_Splitter_even[0]), .pin3(AT_Splitter_even[1]), .pin4(AT_Splitter_even[2]),
    .pin5(AT_Splitter_even[3]), .pin6(1'b0), .pin7(DOTCLOCK), .pin8(1'b0), .pin9(nCLR_SR),
    .pin10(CC_Splitter_even[0]), .pin11(CC_Splitter_even[1]), .pin12(CC_Splitter_even[2]), .pin13(C0),
    .pin14(CC_Splitter_even[3]), .pin15(SL), .pin16(1'b1));
  Seven_Seg_Hex seven_seg_hex_1 (.d({3'b000, RA[4]}), .dp(1'b0));
  Seven_Seg_Hex seven_seg_hex_2 (.d(RA[3:0]), .dp(1'b0));
  // RGBLED rgbled_1: pin names not known; wires that end beside it: RGBI[0], RGBI[1], RGBI[2]
  // _74174 U101: pin names not known; wires that end beside it: _14MHZ, 1'b1, RGBI[0], RGBI[1], RGBI[2], RGBI[3], nRESET_t, U101_p8, 1'b1, 1'b0, R, G_t, B_t, I, U101_p8, nRESET
  // PinControl pincontrol_1: pin names not known; wires that end beside it: pincontrol_1_p1, pincontrol_2_p1[1], 1'b0, pincontrol_1_p4
  // PinControl pincontrol_2: pin names not known; wires that end beside it: pincontrol_2_p1[0], 1'b0, pincontrol_2_p3
  _74166 U8 (
    .pin1(1'b0), .pin2(AT_Splitter_odd[0]), .pin3(AT_Splitter_odd[1]), .pin4(AT_Splitter_odd[2]),
    .pin5(AT_Splitter_odd[3]), .pin6(1'b0), .pin7(DOTCLOCK), .pin8(1'b0), .pin9(nCLR_SR),
    .pin10(CC_Splitter_odd[0]), .pin11(CC_Splitter_odd[1]), .pin12(CC_Splitter_odd[2]), .pin13(C1),
    .pin14(CC_Splitter_odd[3]), .pin15(SL), .pin16(1'b1));
  // PinControl pincontrol_3: pin names not known; wires that end beside it: pincontrol_1_p1, pincontrol_2_p1[3], 1'b0, pincontrol_3_p4
  // PinControl pincontrol_4: pin names not known; wires that end beside it: pincontrol_1_p1, pincontrol_2_p1[2], 1'b0, pincontrol_4_p4
  // PinControl pincontrol_5: pin names not known; wires that end beside it: pincontrol_1_p1, pincontrol_2_p1[5], 1'b0, pincontrol_5_p4
  // PinControl pincontrol_6: pin names not known; wires that end beside it: pincontrol_1_p1, pincontrol_2_p1[4], 1'b0, pincontrol_6_p4
  assign MD_BUS = 1'b0 ? {8{1'b0}} : 8'bz;  // Driver driver_1
  not not_5 (nRESET_t, RESET);
  // PinControl pincontrol_7: pin names not known; wires that end beside it: pincontrol_1_p1, pincontrol_2_p1[7], 1'b0, pincontrol_7_p4, pincontrol_1_p1, pincontrol_2_p1
  // PinControl pincontrol_8: pin names not known; wires that end beside it: pincontrol_1_p1, pincontrol_2_p1[6], 1'b0, pincontrol_8_p4
  // _74374 U58: pin names not known; wires that end beside it: nENCAS_CRT, nRAS, MA_BUS[7], MA_BUS[8], MA_BUS[9], MA_BUS[10], MA_BUS[11], MA12_COND, U58_p9, U58_p10, 1'b1, 1'b0, ADDR_CAS[0], ADDR_CAS[1], ADDR_CAS[2], ADDR_CAS[3], ADDR_CAS[4], ADDR_CAS[6]
  // NotConnected on U58_p9
  // NotConnected on U58_p10
  assign ADDR_CAS[5] = ~nENCAS_CRT ? nHCLK : 1'bz;  // DriverInvSel driverinvsel_1
  not not_6 (pincontrol_1_p1, nIOW);
  and and_2 (and_2_out, AT7, nBLINK_EN);
  Seven_Seg_Hex seven_seg_hex_3 (.d({3'b000, MA12}), .dp(1'b0));
  // _74374 U59: pin names not known; wires that end beside it: nENRAS_CRT, nRAS, MA_BUS[0], MA_BUS[1], MA_BUS[2], MA_BUS[3], MA_BUS[4], MA_BUS[5], MA_BUS[6], U59_p10, 1'b1, 1'b0, ADDR_CAS[0], ADDR_CAS[1], ADDR_CAS[2], ADDR_CAS[3], ADDR_CAS[4], ADDR_CAS[5], ADDR_CAS[6]
  // NotConnected on U59_p10
  // Probe CASADDR on ADDR_CAS
  Seven_Seg_Hex seven_seg_hex_4 (.d(MA_BUS[11:8]), .dp(1'b0));
  Seven_Seg_Hex seven_seg_hex_5 (.d(MA_BUS[7:4]), .dp(1'b0));
  // _74153 U9__74153: pin names not known; wires that end beside it: STR, AT_BUS[2], AT_BUS[6], C1, in_23, STR, AT_BUS[1], AT_BUS[5], C0, in_24, MUX_A, MUX_B, 1'b1, 1'b0, RGBI[0], RGBI[1]
  Seven_Seg_Hex seven_seg_hex_6 (.d(MA_BUS[3:0]), .dp(1'b0));
  // Probe RASADDR on ADDR_CAS
  // Probe RA0 on RA[0]
  and and_3 (and_3_out, nRAS, ~nENRAS_CRT);  // And
  and and_4 (and_4_out, nCAS, ~nENCAS_CRT);  // And
  D_FF #(.Bits(7)) d_ff_1 (.D(ADDR_CAS), .C(~and_3_out), .Q(d_ff_1_q));  // open: nQ
  D_FF #(.Bits(7)) d_ff_2 (.D(ADDR_CAS), .C(~and_4_out), .Q(d_ff_2_q));  // open: nQ
  Seven_Seg_Hex seven_seg_hex_7 (.d({2'b00, d_ff_2_q[6:5]}), .dp(1'b0));
  // _74153 U10__74153: pin names not known; wires that end beside it: STR, AT_BUS[0], AT_BUS[4], SEL_BLUE, in_25, STR, AT_BUS[3], and_2_out, in_21, in_26, MUX_A, MUX_B, 1'b1, 1'b0, RGBI[2], RGBI[3]
  // _74174 U39: pin names not known; wires that end beside it: 1'b0, nRESET_t, 1'b0, 1'b0, 1'b0, 1'b0, 1'b0, 1'b0, 1'b1, 1'b0
  // Probe ENRAS_CRT on nENRAS_CRT
  // Probe ENCAS_CRT on nENCAS_CRT
  Seven_Seg_Hex seven_seg_hex_8 (.d(d_ff_2_q[4:1]), .dp(1'b0));
  Seven_Seg_Hex seven_seg_hex_9 (.d({d_ff_2_q[0], d_ff_1_q[6:4]}), .dp(1'b0));
  // Probe on d_ff_2_q[4:1]
  Seven_Seg_Hex seven_seg_hex_10 (.d(d_ff_1_q[3:0]), .dp(1'b0));
  // Probe on d_ff_1_q[3:0]
  // Probe on {d_ff_2_q[0], d_ff_1_q[6:4]}
  nor nor_1 (nor_1_out, nRESET_t, nRESET_t);
  _74ls393 U12 (
    .CKA(VSYNC_DLY), ._1QC(nCURSOR_BLINK), .VCC(1'b1), .GND(1'b0), ._1CLR(nor_1_out), .CKB(nCURSOR_BLINK),
    ._2QA(nBLINK), ._2CLR(nor_1_out));  // open: _1QA, _1QB, _1QD, _2QB, _2QC, _2QD
  // _74174 U40: pin names not known; wires that end beside it: 1'b0, nRESET_t, 1'b0, 1'b0, 1'b0, 1'b0, 1'b0, 1'b0, 1'b1, 1'b0
  _74125 U62 (
    .pin1(1'b0), .pin2(1'b0), .pin4(1'b0), .pin5(1'b0), .pin7(1'b0), .pin8(U62_pin8), .pin9(SL_t),
    .pin10(1'b0), .pin11(SL), .pin12(U62_pin8), .pin13(1'b0), .pin14(1'b1));  // open: pin3, pin6
  _7408 U13 (
    .pin1(1'b0), .pin2(1'b0), .pin4(1'b0), .pin5(1'b0), .pin7(1'b0), .pin9(1'b0), .pin10(1'b0),
    .pin11(U13_pin11), .pin12(U13_pin12), .pin13(CHGDOTS), .pin14(1'b1));  // open: pin3, pin6, pin8
  nor nor_2 (nor_2_out, nCURSOR_DLY, nCURSOR_BLINK);
  _7432 U14 (
    .pin1(AT_BLINK_GATE), .pin2(nBLINK), .pin3(U13_pin12), .pin4(U13_pin11), .pin5(nor_2_out),
    .pin6(DOTS_ALPHA), .pin7(1'b0), .pin9(1'b1), .pin10(1'b1), .pin12(1'b1), .pin13(1'b1), .pin14(1'b1));  // open: pin8, pin11
  nand nand_2 (HRES_BORDER, in_19, nDISPEN_DLY);
  _7486 U68 (
    .pin1(1'b0), .pin2(1'b0), .pin4(1'b0), .pin5(1'b0), .pin7(1'b0), .pin8(U68_pin8), .pin9(LCLK),
    .pin10(Q4), .pin11(CS_CROM), .pin12(U68_pin8), .pin13(RESET), .pin14(1'b1));  // open: pin3, pin6
  _7404 U16 (
    .pin1(1'b1), .pin3(in_19), .pin4(nHRES_GFX), .pin5(in_20), .pin6(nBLINK_EN), .pin7(1'b0), .pin8(nBW_2),
    .pin9(in_17), .pin10(nGRPH), .pin11(in_16), .pin12(nHRES), .pin13(in_15), .pin14(1'b1));  // open: pin2
  // _7404 U20: pin names not known; wires that end beside it: CURSOR, DEN, U20_p3, RESET, 1'b1, 1'b1, 1'b1, 1'b0, U20_p9, nDEN, SEL_BLUE, nRESET_t
  // _74174 U21: pin names not known; wires that end beside it: U20_p9, HCLK, nDEN, HS, 1'b1, VS, U21_p7, U21_p8, 1'b1, 1'b0, U21_p7, U21_p8, HSYNC_DLY, VSYNC_DLY, nCURSOR_DLY, nDISPEN_DLY
  nand nand_3 (nand_3_out, nDISPEN_DLY, U21_p8);
  nor nor_3 (nSYNC, VSYNC_DLY, HSYNC_DLY);
  and and_5 (nCLR_SR, in_18, nand_3_out);
  isa_slot isa_slot_1 (
    .OSC(OSC), .RESET(RESET), .SA({isa_slot_1_sa, A0}), .nIOW(nIOW), .T_C(isa_slot_1_t_c),
    .SD(isa_slot_1_sd), .IO_READY(1'b1), .IO_CK(1'b0), .PCLK_BUS(clk), .OSC_BUS(clk_2), .RESET_BUS(1'b0),
    .SD_BUS({A2, H, G, F, E, D, C, B}), .DREQ_BUS(Y), .IRQ_BUS(X), .IOREADY_BUS(Z), .IOCHK_BUS(U));  // open: VCC, GND, CLK, ALE, AEN, nIOR, nMEMR, nMEMW, nDACK
  // _7451 U22: pin names not known; wires that end beside it: U22_p1, nHRES_GFX, DOTS_ALPHA, 1'b1, in_16, nGRPH, C0, in_17, in_22, nBW_2, 1'b1, 1'b0, U22_p13, U20_p3
  _7432 U23 (
    .pin1(C0), .pin2(C1), .pin3(U22_p1), .pin4(1'b0), .pin5(1'b0), .pin7(1'b0), .pin8(MUX_A), .pin9(U22_p13),
    .pin10(nDISPEN_DLY), .pin11(MUX_B), .pin12(in_19), .pin13(nDISPEN_DLY), .pin14(1'b1));  // open: pin6
  // _74244 U67: pin names not known; wires that end beside it: R, G_t, B_t, I, 1'b0, HSYNC_DLY, VSYNC_DLY, 1'b0, 1'b0, 1'b0, 1'b1, 1'b0, U67_p13, U67_p14, U67_p15, U67_p16, U67_p17, U67_p18
  Counter #(.Bits(10)) SCANLINE (.en(1'b1), .C(U67_p17), .clr(U67_p18), .out(SCANLINE_out));  // open: ovf
  // Probe on CURSOR
  // Probe on SCANLINE_out
  // Probe FRAME on U67_p18
  dsub dsub_1 (.R(U67_p13), .G(U67_p14), .B(U67_p15), .I(U67_p16), .H(U67_p17), .V(U67_p18), .clk(n14MHZ));
  // also tied to GND on the sheet: {isa_slot_1_t_c, isa_slot_1_sd[0], isa_slot_1_sd[1], isa_slot_1_sd[2], isa_slot_1_sd[3], isa_slot_1_sd[4], isa_slot_1_sd[5], isa_slot_1_sd[6], isa_slot_1_sd[7], RESET}

  // Other names for the same wires on the sheet: MA_BUS[12] = MA12; ADDR_RAS[6:0] = ADDR_CAS; AT_BUS[7] = AT7;
  //   B_OVERSCAN = in_25; BLINK_EN = in_20; BW = in_17; G_OVERSCAN = in_24; GRPH = in_16; HRES = in_15;
  //   HRES_GFX = in_19; I_BACKGROUND = in_21; I_OVERSCAN = in_26; OSC_BUS = clk_2; R_OVERSCAN = in_23;
  //   SEL_COLOR = in_22; VIDEO_EN = in_18

  // Notes on the sheet:
  //   clk_2: Hz: 2147483647
  //   in_15: default 1
  //   in_18: default 1
  //   in_25: default 1
  //   in_26: default 1
  //   RAS/CAS Enable
  //   U46 is responsible from taking inputs from U47 and U1 and synthesizing
  //   the ~ENRAS signals, which are used to enable the relevant address bus drivers.
  //   It is important that only one bus driver drive the data bus at any given time.
  //   RAS/CAS Sync
  //   U25C
  //   U23B
  //   RAS/CAS Generator
  //   This XOR gate combines several of the CGA's clocks in 
  //   order to synthesize the RAS and CAS signals for RAM.
  //   Dot and Character Clock Selector
  //   U27 has the critical role of generating the Dot and
  //   Character Clocks, switching between the pairs of
  //   14Mhz / HCLK and 7Mhz / LCLK depending on the
  //    status of the HRES signal.
  //   Clock Derivation
  //   Two flip-flops derive most of the CGA's clocks by division, feeding outputs back into inputs. 
  //   Each loop divides the source clock by 2.
  //   Character Generator
  //   -
  //   Part of the text blink circuitry.
  //   Blinking must be enabled in the mode 
  //   control register, attrtibute bit 7 must be
  //   set, and no cursor can be visible.
  //   AT_BLINKGATE is gated further elsewhere.
  //   MA12 Control, SL' generation
  //   These two gates handle a variety of functions. 
  //   One output is MA12, which utlizes the GRPH, ~GRPH, and RA0 inputs to determine
  //   whether MA12 should be set - this creates the famous 8k offset for odd scanlines.
  //   U49 also generates the pre-Shift Load signal, SL' used for rasterization timing.
  //   U33: Character ROM
  //   U30C
  //   U34: Character Code Latch
  //   Video Memory
  //   Normally comprised of 8 bit addressable DRAM modules, I've implemented VRAM
  //   as a single 8 bit module for simplicity (and speed). It otherwise works exactly the same.
  //   RAM is addressed by setting a 7 bit row address via the Row Address Strobe (RAS)
  //   followed by a 7 bit column address set via Column Address Strobe (CAS). 
  //   The ~WE pin controls whether the data presented on D is written, or if the stored data
  //   is emitted on Q.  Since we control ~RAS and ~CAS with timed enable signals, we can 
  //   tie these to the same bus.
  //   U42A
  //   U35: Attribute Byte Latch
  //   U31C
  //   U39: Color Control Register
  //   CGA Palette
  //   U12: Blink Generator
  //   The CGA produces its own blink timings for the cursor and 
  //   for blinking text, ticking this dual counter in stages.  
  //   The text ~BLINK signal ends up half the rate of ~CURSOR_BLINK.
  //   U65D
  //   U40: Mode Control Register
  //   The CGA's mode control register directly controls many high level signals.
  //   Some of these signals are not indended to be active at the same time,
  //   which can lead to interesting and undocumented effects.
  //   HRES: Enables timings for high resolution text mode
  //   GRPH: Enables graphics rasterization
  //   BW: Disables the NTSC color burst, selects alternate palette
  //   VE: Disables display within the active display area (overscan still drawn)
  //   HRES_GFX: Enable the high res graphics mode
  //   BLINK_EN: Interpret attribute bit 7 as 'blink' for text
  //   Text Dot Gate
  //   This logic determines whether the dots produced by the  character generator (CHGDOTS)
  //   become visible dots (DOTS_ALPHA) or are suppressed due to blinking.
  //   U49D
  //   U65B
  //   MUX Inputs
  //   SEL_BLUE Inputs
endmodule
