// Digital circuit mc6845.dig as structural Verilog
module mc6845 (
  input  VSS,
  input  VCC,
  input  nRESET,
  input  LPSTB,
  input  CLK,
  input  R_nW,
  input  E,
  input  RS,
  input  nCS,
  input  D7,
  input  D6,
  input  D5,
  input  D4,
  input  D3,
  input  D2,
  input  D1,
  input  D0,
  output MA0,
  output MA1,
  output MA2,
  output MA3,
  output MA4,
  output MA5,
  output MA6,
  output MA7,
  output MA8,
  output MA9,
  output MA10,
  output MA11,
  output MA12,
  output MA13,
  output DEN,
  output CUR,
  output RA0,
  output RA1,
  output RA2,
  output RA3,
  output RA4,
  output HS,
  output VS
);

  mc6845 #(.applicationType("IVERILOG"), .CodeFile("F:\\digital\\projects\\cga\\mc6845_10.v")) u_mc6845 (
    .VSS(VSS), .VCC(VCC), .RESET_n(nRESET), .LPSTB(LPSTB), .CLK(CLK), .RW(R_nW), .E(E), .RS(RS), .CS_n(nCS),
    .MA0(MA0), .MA1(MA1), .MA2(MA2), .MA3(MA3), .MA4(MA4), .MA5(MA5), .MA6(MA6), .MA7(MA7), .MA8(MA8),
    .MA9(MA9), .MA10(MA10), .MA11(MA11), .MA12(MA12), .MA13(MA13), .DE(DEN), .CURSOR(CUR), .RA0(RA0),
    .RA1(RA1), .RA2(RA2), .RA3(RA3), .RA4(RA4), .HS(HS), .VS(VS), .D0(D0), .D1(D1), .D2(D2), .D3(D3),
    .D4(D4), .D5(D5), .D6(D6), .D7(D7));

  // Notes on the sheet:
  //   VSS: pin 1
  //   VCC: pin 20
  //   nRESET: pin 2
  //   LPSTB: pin 3
  //   CLK: pin 21
  //   R_nW: pin 22
  //   E: pin 23
  //   RS: pin 24
  //   nCS: pin 25
  //   MA0: pin 4
  //   MA1: pin 5
  //   MA2: pin 6
  //   MA3: pin 7
  //   MA4: pin 8
  //   MA5: pin 9
  //   MA6: pin 10
  //   MA7: pin 11
  //   MA8: pin 12
  //   MA9: pin 13
  //   MA10: pin 14
  //   MA11: pin 15
  //   MA12: pin 16
  //   MA13: pin 17
  //   DEN: pin 18
  //   CUR: pin 19
  //   RA0: pin 38
  //   RA1: pin 37
  //   RA2: pin 36
  //   RA3: pin 35
  //   RA4: pin 34
  //   D7: pin 26
  //   D6: pin 27
  //   D5: pin 28
  //   D4: pin 29
  //   D3: pin 30
  //   D2: pin 31
  //   D1: pin 32
  //   D0: pin 33
  //   HS: pin 39
  //   VS: pin 40
endmodule
