// Digital circuit mcm4517.dig as structural Verilog
module mcm4517 (
  input  A0,
  input  A1,
  input  A2,
  input  A3,
  input  A4,
  input  A5,
  input  A6,
  input  [2:0] U_SELECT,
  input  D,
  input  nW,
  input  nRAS,
  input  nCAS,
  output Q
);

  wire bitselector_1_out;
  wire [6:0] LATCH_CAS_q, LATCH_RAS_q;
  wire [7:0] demultiplexer_1_out_7, eeprom_1_d;

  D_FF #(.Bits(7)) LATCH_RAS (.D({A6, A5, A4, A3, A2, A1, A0}), .C(~nRAS), .Q(LATCH_RAS_q));  // open: nQ
  D_FF #(.Bits(7)) LATCH_CAS (.D({A6, A5, A4, A3, A2, A1, A0}), .C(~nCAS), .Q(LATCH_CAS_q));  // open: nQ
  EEPROM #(.AddrBits(14), .isProgramMemory("true"), .Bits(8)) eeprom_1 (
    .A({LATCH_CAS_q, LATCH_RAS_q}), .CS(1'b1), .WE(~nW), .OE(1'b1), .D(eeprom_1_d));
  BitSelector #(.Selector_Bits(3)) bitselector_1 (.in(eeprom_1_d), .sel(U_SELECT), .out(bitselector_1_out));
  assign Q = nW ? bitselector_1_out : 1'bz;  // Driver driver_1
  assign eeprom_1_d = ~nW ? demultiplexer_1_out_7 : 8'bz;  // DriverInvSel driverinvsel_1
  // Probe on eeprom_1_d
  Demultiplexer #(.Selector_Bits(3)) demultiplexer_1 (
    .sel(U_SELECT), .in(D), .out_0(demultiplexer_1_out_7[0]), .out_1(demultiplexer_1_out_7[1]),
    .out_2(demultiplexer_1_out_7[2]), .out_3(demultiplexer_1_out_7[3]), .out_4(demultiplexer_1_out_7[4]),
    .out_5(demultiplexer_1_out_7[5]), .out_6(demultiplexer_1_out_7[6]), .out_7(demultiplexer_1_out_7[7]));

  // Notes on the sheet:
  //   A0: pin 5
  //   A1: pin 7
  //   A2: pin 6
  //   A3: pin 12
  //   A4: pin 11
  //   A5: pin 10
  //   A6: pin 13
  //   Q: pin 14
  //   D: pin 2
  //   nRAS: pin 4
  //   nCAS: pin 15
  //   contents of eeprom_1 (hex, n*v repeats v):
  //   1
endmodule
