// Digital circuit mcm4517_8bit.dig as structural Verilog
module mcm4517_8bit (
  input  A0,
  input  A1,
  input  A2,
  input  A3,
  input  A4,
  input  A5,
  input  A6,
  input  [7:0] D,
  input  nW,
  input  nRAS,
  input  nCAS,
  output [7:0] Q
);

  wire [6:0] LATCH_CAS_q, LATCH_RAS_q;
  wire [7:0] eeprom_1_d;

  D_FF #(.Bits(7)) LATCH_RAS (.D({A6, A5, A4, A3, A2, A1, A0}), .C(~nRAS), .Q(LATCH_RAS_q));  // open: nQ
  D_FF #(.Bits(7)) LATCH_CAS (.D({A6, A5, A4, A3, A2, A1, A0}), .C(~nCAS), .Q(LATCH_CAS_q));  // open: nQ
  EEPROM #(.AddrBits(14), .isProgramMemory("true"), .Bits(8)) eeprom_1 (
    .A({LATCH_CAS_q, LATCH_RAS_q}), .CS(1'b1), .WE(~nW), .OE(1'b1), .D(eeprom_1_d));
  assign Q = nW ? eeprom_1_d : 8'bz;  // Driver driver_1
  assign eeprom_1_d = ~nW ? D : 8'bz;  // DriverInvSel driverinvsel_1

  // Notes on the sheet:
  //   A0: pin 5
  //   A1: pin 7
  //   A2: pin 6
  //   A3: pin 12
  //   A4: pin 11
  //   A5: pin 10
  //   A6: pin 13
  //   Q: pin 14
  //   D: pin 2
  //   nRAS: pin 4
  //   nCAS: pin 15
  //   contents of eeprom_1 (hex, n*v repeats v):
  //   1,2b,1,2b,6a,95,84,95,4a,95,fb,4*a4,fb,a4,4a,95,84,95,6a,95,1
  //   ,2b,1,2b,6a,95,84,95,4a,95,fb,a4,a4,95,2,fb,5a,2b,95,84,95,6a
  //   ,a2,2,19,b0,48,1,19,b0,b0,b0,48,48,48,b0,b6,b0,b0,35,a2,2b,a2
  //   ,1f,1f,dd,1,10,95,60,9,9,b0,84,35,82,35,95,1,2b,1,2b,6a,95,84
  //   ,95,4a,95,fb,4*a4,fb,a4,4a,95,84,95,6a,95,1,2b,1,2b,6a,95,84,95
  //   ,4a,95,fb,a4,a4,95,82,4c,a4,85,95,84,dd,1,7f,19,b1,48,1,19,5,5
  //   ,b0,84,84,84,b0,2,b0,b0,35,1,27,82,a2,1f,dd,22,fb,a4,dd,9,9,b0
  //   ,35,1,49,ab,95,fb,4*a4,fb,a4,4a,95,84,95,6a,95,1,2b,1,2b,6a,95
  //   ,35,6a,35,95,fb,a4,a4,35,2b,35,a4,4a,35,4a,35,6a,35,a4,95,2,fb
  //   ,a4,4a,95,1,14,14,19,b0,1f,1f,85,a1,a1,35,48,48,48,95,a1,b0,b0,b0
  //   ,b6,10,95,82,1,60,22,fb,95,dd,9,9,35,1,29,49,85,4a,95,fb,4*a4
  //   ,fb,a4,4a,95,84,95,6a,95,1,2b,1,2b,35,4a,35,95,4a,95,fb,35,2b
  //   ,35,a4,fb,35,84,35,81,35,fb,a4,a4,1,82,85,1,1,6,b1,b0,19,b0,b1
  //   ,1f,1f,e2,1f,dd,1f,1f,1f,1,48,48,48,1,a5,95,a4,95,35,60,22,fb
  //   ,fd,b,a2,a2,2b,81,60,49,35,95,4a,95,fb,4*a4,fb,a4,4a,95,84,95
  //   ,6a,95,1,2b,35,fb,35,95,84,95,4a,35,95,35,a4,a4,35,6a,35,4a,35
  //   ,4a,95,fb,a4,b,1,1,1d,69,b1,b0,2b,19,a4,b1,1f,e2,fb,a5,a4,6a,69
  //   ,84,a5,4*1f,85,a5,1,a4,b0,60,22,6a,82,48,82,82,60,48,60,35,85
  //   ,84,95,4a,95,fb,4*a4,fb,a4,4a,95,84,95,6a,95,35,a4,35,2b,6a,95
  //   ,84,35,95,35,fb,a4,35,1,a,fb,35,84,95,4a,95,fb,1,7f,1d,14,b1,b0
  //   ,2a,2b,dd,95,a4,1f,fd,fb,a5,a4,a5,84,6a,a5,1f,1f,85,e2,19,48,a4
  //   ,1f,b0,60,22,6a,19,48,81,81,60,b0,69,85,35,20,84,95,4a,95,fb,4*a4
  //   ,fb,a4,4a,95,84,95,35,a4,35,2b,1,2b,6a,35,95,35,4a,95,35,1,35
  //   ,a4,35,6a,95,84,7d,4a,10,2,1d,14,b0,b0,b0,2a,2a,fb,a4,95,1,48
  //   ,fb,a5,a4,6a,69,84,a5,1f,1f,85,1,1f,1f,1,1,b0,60,22,10,19,48,48,48
  //   ,60,b0,85,35,85,a4,4a,95,84,95,6a,95,1,2b,1,2b,6a,95,84,95,4a
  //   ,95,fb,4*a4,fb,a4,4a,95,84,95,6a,95,1,2b,1,2b,6a,5c,84,95,4a,1
  //   ,14,b1,1f,1f,b,2a,2a,95,fb,a4,95,48,fb,35,a4,a5,84,6a,a5,1f,1f,1f
  //   ,85,4*1f,b0,60,22,b0,b0,b0,2a,b0,b0,35,35,85,35,fb,a4,4a,95,84
  //   ,95,6a,95,1,2b,1,2b,6a,95,84,95,4a,95,fb,4*a4,fb,a4,4a,95,84,95
  //   ,6a,95,1,2b,1,a2,6a,95,35,1,1d,b0,35,a4,95,10,1f,1f,1f,95,fb,35
  //   ,60,10,a5,a4,85,69,1,a5,1f,85,dd,1,1f,1f,95,1f,b0,81,81,5,1,35
  //   ,1,a4,b0,7b,dd,35,85,a4,fb,a4,4a,95,84,95,6a,95,1,2b,1,2b,6a,95
  //   ,84,95,4a,95,fb,4*a4,fb,a4,4a,95,84,95,6a,95,1,2b,1,95,25,b,1,1
  //   ,b0,b1,b6,60,81,1f,1f,95,95,95,2b,60,95,1,a4,48,48,48,85,b0,b0
  //   ,dd,1f,1f,95,85,35,b0,81,81,a1,11,35,1f,95,95,60,60,22,35,a4,a4
  //   ,fb,a4,4a,95,84,95,6a,95,1,2b,1,2b,6a,95,84,95,4a,95,fb,4*a4,fb
  //   ,a4,4a,95,84,95,6a,95,1,2b,1,95,1,9f,84,1,b0,b0,60,60,95,1f,95,95,95
  //   ,60,35,35,35,95,81,81,81,b0,1f,a2,35,a5,35,85,35,b0,b0,81,81,5
  //   ,dd,dd,b0,b,10,60,60,22,60,a4,a4,a4,fb,a4,4a,95,84,95,6a,95,1
  //   ,2b,1,2b,6a,95,84,95,4a,95,fb,4*a4,fb,a4,4a,95,84,95,6a,95,1,2b
  //   ,82,1,10,95,5c,1,b0,60,35,dd,a2,fb,95,95,60,2f,35,35,85,48,48
  //   ,1f,1f,dd,82,a1,85,60,35,85,b0,b0,81,81,a1,dd,dd,b0,dd,95,60,60
  //   ,22,60,4*a4,fb,a4,4a,95,84,95,6a,95,1,2b,1,95,6a,95,84,95,4a,95
  //   ,fb,4*a4,fb,a4,4a,95,84,95,6a,95,1,2b,fb,1,95,92,95,6,60,60,2f
  //   ,10,95,35,dd,60,ab,35,85,35,64,48,ae,1f,95,1,35,85,13,49,1,3,13
  //   ,81,81,1,b,10,a5,85,1,60,81,22,b0,fb,4*a4,fb,a4,4a,82,95,95,b
  //   ,e2,1,2b,b,e3,6a,95,84,95,4a,95,fb,a4,24,a4,a4,fb,a4,4a,95,84
  //   ,95,6a,95,1,2b,b,1,b,dd,7f,60,48,fb,b,ae,22,dd,60,22,5b,35,35
  //   ,64,60,35,81,95,35,85,35,2,60,84,1f,13,81,81,95,b0,a4,1,35,b0
  //   ,69,1,22,1,95,fb,4*a4,fb,a4,64,95,99,95,1,a4,1,2b,a4,b,6a,95,84
  //   ,a1,95,95,fb,b,a1,a4,a4,fb,a4,4a,a4,84,95,6a,95,1,2b,10,ab,b,1
  //   ,60,48,dd,95,ae,22,dd,1,22,27,2b,1,6a,48,b0,48,dd,85,35,84,1,a2
  //   ,84,1f,13,48,3,10,95,b0,84,b0,b1,1,1,4a,1,4a,95,fb,a4,a4,a4,a2
  //   ,fb,a4,64,95,1,dd,95,e3,1,b,a2,1f,6a,95,84,2,4a,95,fb,10,a4,a4,a4
  //   ,fb,a4,b,95,dd,e3,dd,95,1,2b,95,1,35,85,48,95,a4,95,1f,a4,81,81,81
  //   ,49,81,95,84,b0,48,dd,b0,84,84,1,82,84,1f,1f,a4,a2,95,81,27,48
  //   ,95,95,1,1,dd,10,95,4a,95,fb,a4,a4,a4,95,95,a4,4a,95,10,2b,10
  //   ,b,1,b,2,e2,6a,95,10,b,4a,95,fb,6a,a4,a4,a4,fb,a4,a4,1,a4,a1,fb
  //   ,95,a2,85,35,85,35,85,b0,95,1f,1f,a4,81,1f,1f,1f,81,81,95,b0,48
  //   ,dd,1,19,35,1f,95,84,b0,b0,fd,a1,95,48,27,b0,1,95,95,1,19,4a,84
  //   ,95,4a,95,fb,a4,a4,85,1,fb,a4,85,1,1,85,1,b,10,1,1,95,2,95,1,1f
  //   ,4a,1f,fb,4*a4,fb,a4,95,b,e3,1,a1,1,35,85,35,85,35,1f,35,1f,1f
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endmodule
