// Digital circuit mcm4517_8bit_multiplexed.dig as structural Verilog
module mcm4517_8bit_multiplexed (
  input  A0,
  input  A1,
  input  A2,
  input  A3,
  input  A4,
  input  A5,
  input  A6,
  input  [7:0] D,
  input  nW,
  input  nRAS,
  input  nCAS,
  input  [2:0] SEL_RAM,
  output [7:0] Q
);

  wire decoder_1_out_0, decoder_1_out_1, decoder_1_out_2, decoder_1_out_3;
  wire [6:0] LATCH_CAS_q, LATCH_RAS_q;
  wire [7:0] eeprom_1_d;

  D_FF #(.Bits(7)) LATCH_RAS (.D({A6, A5, A4, A3, A2, A1, A0}), .C(~nRAS), .Q(LATCH_RAS_q));  // open: nQ
  D_FF #(.Bits(7)) LATCH_CAS (.D({A6, A5, A4, A3, A2, A1, A0}), .C(~nCAS), .Q(LATCH_CAS_q));  // open: nQ
  Decoder #(.Selector_Bits(3)) decoder_1 (
    .sel(SEL_RAM), .out_0(decoder_1_out_0), .out_1(decoder_1_out_1), .out_2(decoder_1_out_2),
    .out_3(decoder_1_out_3));  // open: out_4, out_5, out_6, out_7
  EEPROM #(.AddrBits(14), .isProgramMemory("true"), .Bits(8)) eeprom_1 (
    .A({LATCH_CAS_q, LATCH_RAS_q}), .CS(decoder_1_out_0), .WE(~nW), .OE(decoder_1_out_0), .D(eeprom_1_d));
  EEPROM #(.AddrBits(14), .isProgramMemory("true"), .Bits(8)) eeprom_2 (
    .A({LATCH_CAS_q, LATCH_RAS_q}), .CS(decoder_1_out_1), .WE(~nW), .OE(decoder_1_out_1), .D(eeprom_1_d));
  EEPROM #(.AddrBits(14), .isProgramMemory("true"), .Bits(8)) eeprom_3 (
    .A({LATCH_CAS_q, LATCH_RAS_q}), .CS(decoder_1_out_2), .WE(~nW), .OE(decoder_1_out_2), .D(eeprom_1_d));
  EEPROM #(.AddrBits(14), .isProgramMemory("true"), .Bits(8)) eeprom_4 (
    .A({LATCH_CAS_q, LATCH_RAS_q}), .CS(decoder_1_out_3), .WE(~nW), .OE(decoder_1_out_3), .D(eeprom_1_d));
  assign Q = nW ? eeprom_1_d : 8'bz;  // Driver driver_1
  assign eeprom_1_d = ~nW ? D : 8'bz;  // DriverInvSel driverinvsel_1

  // Notes on the sheet:
  //   A0: pin 5
  //   A1: pin 7
  //   A2: pin 6
  //   A3: pin 12
  //   A4: pin 11
  //   A5: pin 10
  //   A6: pin 13
  //   Q: pin 14
  //   D: pin 2
  //   nRAS: pin 4
  //   nCAS: pin 15
  //   SEL_RAM: Select from one of eight RAM presets.
  //   contents of eeprom_1 (hex, n*v repeats v):
  //   0,4095*2,4096*3f,4096*2,4096*3f
  //   contents of eeprom_2 (hex, n*v repeats v):
  //   0,4095*2,4096*3f,4096*2,4096*3f
  //   contents of eeprom_3 (hex, n*v repeats v):
  //   0,4095*2,4096*3f,4096*2,4096*3f
  //   contents of eeprom_4 (hex, n*v repeats v):
  //   0,4095*2,4096*3f,4096*2,4096*3f
endmodule
