// Digital circuit mk36000.dig as structural Verilog
module mk36000 (
  input  nCE,
  input  A0,
  input  A1,
  input  A2,
  input  A3,
  input  A4,
  input  A5,
  input  A6,
  input  A7,
  input  A8,
  input  A9,
  input  A10,
  input  A11,
  input  A12,
  input  VCC,
  input  GND,
  output D0,
  output D1,
  output D2,
  output D3,
  output D4,
  output D5,
  output D6,
  output D7
);

  ROM #(.AddrBits(13), .Bits(8)) MK36000 (
    .A({A12, A11, A10, A9, A8, A7, A6, A5, A4, A3, A2, A1, A0}), .sel(nCE),
    .D({D7, D6, D5, D4, D3, D2, D1, D0}));
  PowerSupply powersupply_1 (.VDD(VCC), .GND(GND));

  // Notes on the sheet:
  //   nCE: pin 20
  //   A0: pin 8
  //   A1: pin 7
  //   A2: pin 6
  //   A3: pin 5
  //   A4: pin 4
  //   A5: pin 3
  //   A6: pin 2
  //   A7: pin 1
  //   A8: pin 23
  //   A9: pin 22
  //   A10: pin 19
  //   A11: pin 18
  //   A12: pin 21
  //   D0: pin 9
  //   D1: pin 10
  //   D2: pin 12
  //   D3: pin 13
  //   D4: pin 14
  //   D5: pin 15
  //   D6: pin 16
  //   D7: pin 17
  //   VCC: pin 24, default 1
  //   GND: pin 12
  //   contents of MK36000 (hex, n*v repeats v):
  //   10*0,7e,81,a5,81,81,bd,0,0,7e,ff,db,ff,ff,c3,0,0,0,36,4*7f,0,0,0
  //   ,8,1c,3e,7f,3e,0,0,18,3c,3c,e7,e7,e7,0,0,18,3c,7e,ff,ff,7e,5*0
  //   ,18,3c,3c,5*ff,e7,c3,c3,4*0,3c,66,42,42,4*ff,c3,99,bd,bd,0,0,f
  //   ,7,d,19,3c,66,0,0,3c,66,66,66,3c,18,0,0,3f,33,3f,30,30,30,0,0
  //   ,7f,63,7f,63,63,63,0,0,18,18,db,3c,e7,3c,0,0,40,60,70,7c,7f,7c
  //   ,0,0,1,3,7,1f,7f,1f,0,0,18,3c,7e,18,18,18,0,0,6*33,0,0,7f,db,db,db
  //   ,7b,1b,0,3e,63,30,1c,36,63,63,10*0,18,3c,7e,18,18,18,0,0,18,3c
  //   ,7e,18,18,18,0,0,6*18,4*0,c,6,7f,6,4*0,18,30,7f,30,5*0,60,60,60
  //   ,4*0,24,66,ff,66,0,0,0,8,1c,1c,3e,3e,0,0,0,7f,7f,3e,3e,1c,10*0
  //   ,18,3c,3c,3c,18,18,0,63,63,63,22,5*0,36,36,7f,36,36,36,c,c,3e
  //   ,63,61,60,3e,3,4*0,61,63,6,c,0,0,1c,36,36,1c,3b,6e,0,30,30,30
  //   ,60,5*0,c,18,4*30,0,0,18,c,4*6,4*0,66,3c,ff,3c,0,0,0,18,18,18
  //   ,ff,18,14*0,ff,11*0,1,3,6,c,18,30,0,0,3e,63,67,6f,7b,73,0,0,c
  //   ,1c,3c,c,c,c,0,0,3e,63,3,6,c,18,0,0,3e,63,3,3,1e,3,0,0,6,e,1e
  //   ,36,66,7f,0,0,7f,60,60,60,7e,3,0,0,1c,30,60,60,7e,63,0,0,7f,63
  //   ,3,6,c,18,0,0,3e,63,63,63,3e,63,0,0,3e,63,63,63,3f,3,0,0,0,18,18
  //   ,6*0,18,18,5*0,6,c,18,30,60,30,5*0,7e,4*0,60,30,18,c,6,c,0,0,3e
  //   ,63,63,6,c,c,0,0,3e,63,63,6f,6f,6f,0,0,8,1c,36,63,63,7f,0,0,7e
  //   ,33,33,33,3e,33,0,0,1e,33,61,60,60,60,0,0,7c,36,4*33,0,0,7f,33
  //   ,31,34,3c,34,0,0,7f,33,31,34,3c,34,0,0,1e,33,61,60,60,6f,0,0,4*63
  //   ,7f,63,0,0,3c,5*18,0,0,f,5*6,0,0,73,33,36,36,3c,36,0,0,78,5*30
  //   ,0,0,c3,e7,ff,db,c3,c3,0,0,63,73,7b,7f,6f,67,0,0,1c,36,4*63,0,0
  //   ,7e,33,33,33,3e,30,0,0,3e,4*63,6b,0,0,7e,33,33,33,3e,36,0,0,3e
  //   ,63,63,30,1c,6,0,0,ff,db,99,18,18,18,0,0,6*63,0,0,6*c3,0,0,4*c3
  //   ,db,db,0,0,c3,c3,66,3c,18,3c,0,0,c3,c3,c3,66,3c,18,0,0,ff,c3,86
  //   ,c,18,30,0,0,3c,5*30,0,0,40,60,70,38,1c,e,0,0,3c,5*c,8,1c,36,63
  //   ,12*0,18,18,c,10*0,3c,6,3e,0,0,70,30,30,3c,36,33,5*0,3e,63,60
  //   ,0,0,e,6,6,1e,36,66,5*0,3e,63,7f,0,0,1c,36,32,30,7c,30,5*0,3b
  //   ,66,66,0,0,70,30,30,36,3b,33,0,0,c,c,0,1c,c,c,0,0,6,6,0,e,6,6
  //   ,0,0,70,30,30,33,36,3c,0,0,1c,5*c,5*0,e6,ff,db,5*0,6e,33,33,5*0
  //   ,3e,63,63,5*0,6e,33,33,5*0,3b,66,66,5*0,6e,3b,33,5*0,3e,63,38
  //   ,0,0,8,18,18,7e,18,18,5*0,66,66,66,5*0,c3,c3,c3,5*0,c3,c3,db,5*0
  //   ,63,36,1c,5*0,63,63,63,5*0,7f,66,c,0,0,e,18,18,18,70,18,0,0,4*18
  //   ,0,18,0,0,70,18,18,18,e,18,0,0,3b,6e,8*0,8,1c,36,63,0,0,1e,33
  //   ,61,60,60,61,0,0,66,66,0,66,66,66,0,6,c,18,0,3e,63,7f,0,8,1c,36
  //   ,0,3c,6,3e,0,0,66,66,0,3c,6,3e,0,30,18,c,0,3c,6,3e,0,1c,36,1c
  //   ,0,3c,6,3e,4*0,3c,66,60,66,0,8,1c,36,0,3e,63,7f,0,0,66,66,0,3e
  //   ,63,7f,0,30,18,c,0,3e,63,7f,0,0,66,66,0,38,18,18,0,18,3c,66,0
  //   ,38,18,18,0,60,30,18,0,38,18,18,0,63,63,8,1c,36,63,63,1c,36,1c
  //   ,0,1c,36,63,63,c,18,30,0,7f,33,30,3e,4*0,6e,3b,1b,7e,0,0,1f,36
  //   ,66,66,7f,66,0,8,1c,36,0,3e,63,63,0,0,63,63,0,3e,63,63,0,30,18
  //   ,c,0,3e,63,63,0,18,3c,66,0,66,66,66,0,30,18,c,0,66,66,66,0,0,63,63
  //   ,0,63,63,63,0,63,63,1c,36,63,63,63,0,63,63,0,4*63,0,18,18,7e,c3
  //   ,c0,c0,c3,0,1c,36,32,30,78,30,30,0,0,c3,66,3c,18,ff,18,0,fc,66,66
  //   ,7c,62,66,6f,0,e,1b,18,18,18,7e,18,0,c,18,30,0,3c,6,3e,0,c,18
  //   ,30,0,38,18,18,0,c,18,30,0,3e,63,63,0,c,18,30,0,66,66,66,0,0,3b
  //   ,6e,0,6e,33,33,3b,6e,0,63,73,7b,7f,6f,0,3c,6c,6c,3e,0,7e,0,0,38
  //   ,6c,6c,38,0,7c,0,0,0,18,18,0,18,18,30,6*0,7f,60,6*0,7f,3,0,60
  //   ,e0,63,66,6c,18,30,0,60,e0,63,66,6c,18,33,0,0,18,18,0,18,18,3c
  //   ,4*0,1b,36,6c,36,4*0,6c,36,1b,36,11,44,11,44,11,44,11,44,55,aa
  //   ,55,aa,55,aa,55,aa,dd,77,dd,77,dd,77,dd,77,15*18,f8,5*18,f8,18
  //   ,f8,7*36,f6,7*0,fe,5*0,f8,18,f8,5*36,f6,6,f6,8*36,5*0,fe,6,f6
  //   ,5*36,f6,6,fe,7*36,fe,5*18,f8,18,f8,7*0,f8,7*18,1f,7*18,ff,7*0
  //   ,ff,7*18,1f,7*0,ff,7*18,ff,5*18,1f,18,1f,7*36,37,5*36,37,30,3f
  //   ,5*0,3f,30,37,5*36,f7,0,ff,5*0,ff,0,f7,5*36,37,30,37,5*0,ff,0
  //   ,ff,5*36,f7,0,f7,5*18,ff,0,ff,7*36,ff,5*0,ff,0,ff,7*0,ff,7*36
  //   ,3f,5*18,1f,18,1f,5*0,1f,18,1f,7*0,3f,7*36,ff,5*18,ff,18,ff,7*18
  //   ,f8,7*0,1f,8*ff,7*0,ff,8*f0,8*f,7*ff,6*0,3b,6e,6c,4*0,3e,63,7e
  //   ,63,0,0,7f,63,63,60,60,60,4*0,7f,36,36,36,0,0,7f,63,30,18,c,18
  //   ,5*0,3f,6c,6c,4*0,4*33,4*0,3b,6e,c,c,0,0,7e,18,3c,66,66,66,0,0
  //   ,1c,36,63,63,7f,63,0,0,1c,36,63,63,63,36,0,0,1e,30,18,c,3e,66
  //   ,5*0,7e,db,db,0,0,3,6,7e,db,db,f3,0,0,1c,30,60,60,7c,60,0,0,0
  //   ,3e,4*63,0,0,0,7f,0,0,7f,0,0,0,18,18,18,ff,18,18,0,0,30,18,c,6
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endmodule
