// Digital circuit odd_even_splitter.dig as structural Verilog
module odd_even_splitter (
  input  [7:0] BYTE_IN,
  output [3:0] ODD,
  output [3:0] EVEN
);


  assign EVEN = {BYTE_IN[6], BYTE_IN[4], BYTE_IN[2], BYTE_IN[0]};
  assign ODD = {BYTE_IN[7], BYTE_IN[5], BYTE_IN[3], BYTE_IN[1]};
endmodule
