// Digital circuit strobe_logic.dig as structural Verilog
module strobe_logic (
  input  CLOCK_DOT,
  input  VSYNC_DLY,
  input  HSYNC_DLY,
  input  HRES_GFX,
  input  C0,
  input  C1,
  output STR
);

  wire and_1_out, and_2_out, nand_1_out, nand_2_out, nor_1_out, nor_2_out, not_1_out, not_2_out, not_3_out,
       not_4_out, or_1_out;

  nor nor_1 (nor_1_out, VSYNC_DLY, HSYNC_DLY);
  not not_1 (not_1_out, CLOCK_DOT);
  nand nand_1 (nand_1_out, not_1_out, nand_2_out);
  nand nand_2 (nand_2_out, nand_1_out, CLOCK_DOT);
  and and_1 (and_1_out, C0, nand_1_out);
  and and_2 (and_2_out, nand_2_out, C1);
  nor nor_2 (nor_2_out, and_1_out, and_2_out);
  not not_2 (not_2_out, nor_2_out);
  not not_3 (not_3_out, HRES_GFX);
  or or_1 (or_1_out, not_2_out, not_3_out);
  nand nand_3 (STR, nor_1_out, or_1_out);
  not not_4 (not_4_out, STR);
  LED Video_Output (.in(not_4_out));

  // Notes on the sheet:
  //   HRES_GFX: default 1
endmodule
