// Digital circuit sync_timings.dig as structural Verilog
module sync_timings (
  input  VSYNC_DLY,
  input  HSYNC_DLY,
  input  LCLK,
  output VSYNC_OUT
);

  wire nand_1_out, U63_pin2, U63_pin7, U63_pin10, U63_pin14, U64_pin1, U64_pin4, U64_pin6, U64_pin13;

  _74164 U64 (
    .pin1(U64_pin1), .pin2(1'b1), .pin4(U64_pin4), .pin6(U64_pin6), .pin7(1'b0), .pin8(LCLK),
    .pin9(HSYNC_DLY), .pin13(U64_pin13), .pin14(1'b1));  // open: pin3, pin5, pin10, pin11, pin12
  _74175 U63 (
    .pin1(VSYNC_DLY), .pin2(U63_pin2), .pin4(1'b1), .pin5(U63_pin2), .pin7(U63_pin7), .pin8(1'b0),
    .pin9(U64_pin4), .pin10(U63_pin10), .pin12(U63_pin7), .pin13(U63_pin10), .pin14(U63_pin14), .pin16(1'b1));  // open: pin3, pin6, pin11, pin15
  and and_1 (VSYNC_OUT, U63_pin2, U63_pin14);
  nand nand_1 (nand_1_out, U64_pin13, U64_pin13);
  xor xor_1 (U64_pin1, nand_1_out, U64_pin6);

  // Notes on the sheet:
  //   U41C
  //   U15B
  //   U42C
endmodule
